// Logisim project 16-bit_D-FlipFlop.circ as structural Verilog: 1 circuit, main circuit main
module main (
  input  E,
  input  CLK,
  input  [15:0] I,
  output [15:0] O
);

  Hex_Digit_Display hex_digit_display_1 (.value(I[15:12]));  // open: dp
  Hex_Digit_Display hex_digit_display_2 (.value(I[7:4]));  // open: dp
  Hex_Digit_Display hex_digit_display_3 (.value(I[11:8]));  // open: dp
  Hex_Digit_Display hex_digit_display_4 (.value(I[3:0]));  // open: dp
  _8_bit_D_FlipFlop_main main_1 (.I(I[7:0]), .E(E), .CLK(CLK), .O(O[7:0]));
  _8_bit_D_FlipFlop_main main_2 (.I(I[15:8]), .E(E), .CLK(CLK), .O(O[15:8]));
  Hex_Digit_Display hex_digit_display_5 (.value(O[11:8]));  // open: dp
  Hex_Digit_Display hex_digit_display_6 (.value(O[15:12]));  // open: dp
  Hex_Digit_Display hex_digit_display_7 (.value(O[7:4]));  // open: dp
  Hex_Digit_Display hex_digit_display_8 (.value(O[3:0]));  // open: dp
endmodule
