// Logisim project 8-bit_Adder_Subtractor.circ as structural Verilog: 1 circuit, main circuit main
module main (
  input  Adder_Subtractor,
  input  [7:0] B,
  input  [7:0] A,
  output [7:0] O,
  output Cout
);

  wire [7:0] xor_1_out;

  Hex_Digit_Display hex_digit_display_1 (.value(B[7:4]));  // open: dp
  Hex_Digit_Display hex_digit_display_2 (.value(B[3:0]));  // open: dp
  Hex_Digit_Display hex_digit_display_3 (.value(A[7:4]));  // open: dp
  Hex_Digit_Display hex_digit_display_4 (.value(A[3:0]));  // open: dp
  assign xor_1_out = {8{Adder_Subtractor}} ^ B;  // XOR_Gate xor_1, 8 bits wide
  Adder adder_1 (.a(xor_1_out), .b(A), .out(O), .cin(Adder_Subtractor), .cout(Cout));
  Hex_Digit_Display hex_digit_display_5 (.value(O[7:4]));  // open: dp
  Hex_Digit_Display hex_digit_display_6 (.value(O[3:0]));  // open: dp
endmodule
