// Logisim project 8-bit_GeneralRegisterFile(Part2a).circ as structural Verilog: 1 circuit, main circuit main
module main (
  input  [3:0] TempSel,
  input  [3:0] RegSel,
  input  CLK,
  input  [1:0] FunSel,
  input  [7:0] Input,
  input  [2:0] OutASel,
  input  [2:0] OutBSel,
  output [7:0] OutA,
  output [7:0] OutB
);

  wire [3:0] not_1_out, not_2_out;
  wire [7:0] R1_q, R2_q, R3_q, R4_q, T1_q, T2_q, T3_q, T4_q;

  Hex_Digit_Display hex_digit_display_1 (.value(Input[7:4]));  // open: dp
  Hex_Digit_Display hex_digit_display_2 (.value(Input[3:0]));  // open: dp
  assign not_1_out = ~RegSel;  // NOT_Gate not_1, 4 bits wide
  _8_bit_Register_Part1a__main R1 (.FunSel(FunSel), .I(Input), .E(not_1_out[3]), .CLK(CLK), .Q(R1_q));
  _8_bit_Register_Part1a__main R2 (.FunSel(FunSel), .I(Input), .E(not_1_out[2]), .CLK(CLK), .Q(R2_q));
  _8_bit_Register_Part1a__main R3 (.FunSel(FunSel), .I(Input), .E(not_1_out[1]), .CLK(CLK), .Q(R3_q));
  _8_bit_Register_Part1a__main R4 (.FunSel(FunSel), .I(Input), .E(not_1_out[0]), .CLK(CLK), .Q(R4_q));
  Multiplexer #(.select(3), .width(8), .enable("false")) multiplexer_1 (
    .in0(R1_q), .in1(R2_q), .in2(R3_q), .in3(R4_q), .in4(T1_q), .in5(T2_q), .in6(T3_q), .in7(T4_q),
    .out(OutA), .sel(OutASel));
  Multiplexer #(.select(3), .width(8), .enable("false")) multiplexer_2 (
    .in0(R1_q), .in1(R2_q), .in2(R3_q), .in3(R4_q), .in4(T1_q), .in5(T2_q), .in6(T3_q), .in7(T4_q),
    .out(OutB), .sel(OutBSel));
  _8_bit_Register_Part1a__main T1 (.FunSel(FunSel), .I(Input), .E(not_2_out[3]), .CLK(CLK), .Q(T1_q));
  _8_bit_Register_Part1a__main T2 (.FunSel(FunSel), .I(Input), .E(not_2_out[2]), .CLK(CLK), .Q(T2_q));
  Hex_Digit_Display hex_digit_display_3 (.value(OutA[7:4]));  // open: dp
  Hex_Digit_Display hex_digit_display_4 (.value(OutB[7:4]));  // open: dp
  _8_bit_Register_Part1a__main T3 (.FunSel(FunSel), .I(Input), .E(not_2_out[1]), .CLK(CLK), .Q(T3_q));
  Hex_Digit_Display hex_digit_display_5 (.value(OutA[3:0]));  // open: dp
  Hex_Digit_Display hex_digit_display_6 (.value(OutB[3:0]));  // open: dp
  _8_bit_Register_Part1a__main T4 (.FunSel(FunSel), .I(Input), .E(not_2_out[0]), .CLK(CLK), .Q(T4_q));
  assign not_2_out = ~TempSel;  // NOT_Gate not_2, 4 bits wide
endmodule
