// Logisim project 8-bit_Register(Part1a).circ as structural Verilog: 1 circuit, main circuit main
module main (
  input  E,
  input  CLK,
  input  [1:0] FunSel,
  input  [7:0] I,
  output [7:0] Q
);

  wire not_1_out;
  wire [7:0] Adder_Subtractor_o, multiplexer_1_out;

  Hex_Digit_Display hex_digit_display_1 (.value(I[7:4]));  // open: dp
  Hex_Digit_Display hex_digit_display_2 (.value(I[3:0]));  // open: dp
  not not_1 (not_1_out, FunSel[0]);
  _8_bit_Adder_Subtractor_main Adder_Subtractor (
    .Adder_Subtractor(not_1_out), .B(8'h1), .A(Q), .O(Adder_Subtractor_o));  // open: Cout
  Multiplexer #(.select(2), .width(8)) multiplexer_1 (
    .in0(Adder_Subtractor_o), .in1(Adder_Subtractor_o), .in2(I), .in3({8{1'b0}}), .out(multiplexer_1_out),
    .sel(FunSel), .en(E));
  _8_bit_D_FlipFlop_main _8_bit_D_FF (.I(multiplexer_1_out), .E(E), .CLK(CLK), .O(Q));
  Hex_Digit_Display hex_digit_display_3 (.value(Q[7:4]));  // open: dp
  Hex_Digit_Display hex_digit_display_4 (.value(Q[3:0]));  // open: dp
endmodule
