// Logisim project ALUSystem(Part3).circ as structural Verilog: 10 circuits, main circuit ALUSystem
// OutAlu
module ALUSystem (
  input  CLK,
  input  [7:0] A,
  input  [7:0] B,
  input  [3:0] FunSel,
  output [3:0] ZCNO,
  output [7:0] OutALU
);

  wire [3:0] alu_1_zcno;

  Hex_Digit_Display hex_digit_display_1 (.value(A[3:0]));  // open: dp
  Hex_Digit_Display hex_digit_display_2 (.value(A[7:4]));  // open: dp
  Hex_Digit_Display hex_digit_display_3 (.value(B[7:4]));  // open: dp
  Hex_Digit_Display hex_digit_display_4 (.value(B[3:0]));  // open: dp
  ALU alu_1 (.A(A), .B(B), .Cin(ZCNO[2]), .ZCNO(alu_1_zcno), .Output(OutALU), .FunSel(FunSel));
  ZCNO zcno_1 (.ZCNO_IN(alu_1_zcno), .CLK(CLK), .ZCNO_OUT(ZCNO));
  Hex_Digit_Display hex_digit_display_5 (.value(OutALU[3:0]));  // open: dp
  Hex_Digit_Display hex_digit_display_6 (.value(OutALU[7:4]));  // open: dp
endmodule

module ALU (
  input  [7:0] A,
  input  [7:0] B,
  input  Cin,
  input  [3:0] FunSel,
  output [3:0] ZCNO,
  output [7:0] Output
);

  wire [3:0] arithmeticleftshift_1_overflow, arithmeticunit_1_overflow, undriven, undriven_2, undriven_3,
       undriven_4, undriven_5, undriven_6, undriven_7, undriven_8;
  wire [7:0] arithmeticleftshift_1_out, arithmeticrightshift_1_out, arithmeticunit_1_out,
       circularshift_1_out, logicalshift_1_out, logicunit_1_out, not_2_out, not_3_out;

  Hex_Digit_Display hex_digit_display_1 (.value(A[7:4]));  // open: dp
  Hex_Digit_Display hex_digit_display_2 (.value(A[3:0]));  // open: dp
  Hex_Digit_Display hex_digit_display_3 (.value(B[3:0]));  // open: dp
  Hex_Digit_Display hex_digit_display_4 (.value(B[7:4]));  // open: dp
  ZeroDetector zerodetector_1 (.In(A), .Zero(undriven[3]));
  ZeroDetector zerodetector_2 (.In(B), .Zero(undriven_2[3]));
  not not_1 (undriven_3[1], B[7]);
  assign not_2_out = ~A;  // NOT_Gate not_2, 8 bits wide
  assign not_3_out = ~B;  // NOT_Gate not_3, 8 bits wide
  not not_4 (undriven_4[1], A[7]);
  ZeroDetector zerodetector_3 (.In(not_2_out), .Zero(undriven_4[3]));
  ZeroDetector zerodetector_4 (.In(not_3_out), .Zero(undriven_3[3]));
  ArithmeticUnit arithmeticunit_1 (
    .Cin(Cin), .SEL(FunSel[1:0]), .A(A), .B(B), .Out(arithmeticunit_1_out),
    .Zero(arithmeticunit_1_overflow[3]), .Negative(arithmeticunit_1_overflow[1]),
    .Overflow(arithmeticunit_1_overflow[0]), .Carry(arithmeticunit_1_overflow[2]));
  LogicUnit logicunit_1 (
    .A(A), .B(B), .SEL(FunSel[1:0]), .Out(logicunit_1_out), .Zero(undriven_5[3]), .Negative(undriven_5[1]));
  LogicalShift logicalshift_1 (
    .A(A), .LR(FunSel[0]), .Out(logicalshift_1_out), .Zero(undriven_6[3]), .Negative(undriven_6[1]),
    .Carry(undriven_6[2]));
  ArithmeticLeftShift arithmeticleftshift_1 (
    .A(A), .Out(arithmeticleftshift_1_out), .Zero(arithmeticleftshift_1_overflow[3]),
    .Negative(arithmeticleftshift_1_overflow[1]), .Overflow(arithmeticleftshift_1_overflow[0]));
  ArithmeticRightShift arithmeticrightshift_1 (.A(A), .Out(arithmeticrightshift_1_out), .Zero(undriven_7[3]));
  CircularShift circularshift_1 (
    .A(A), .LR(FunSel[0]), .Out(circularshift_1_out), .Zero(undriven_8[3]), .Negative(undriven_8[1]),
    .Carry(undriven_8[2]));
  Multiplexer #(.select(4), .width(4), .enable("false")) multiplexer_1 (
    .in0({undriven[3:2], A[7], undriven[0]}), .in1({undriven_2[3:2], B[7], undriven_2[0]}), .in2(undriven_4),
    .in3(undriven_3), .in4(arithmeticunit_1_overflow), .in5(arithmeticunit_1_overflow),
    .in6(arithmeticunit_1_overflow), .in7(undriven_5), .in8(undriven_5), .in9(undriven_5), .in10(undriven_6),
    .in11(undriven_6), .in12(arithmeticleftshift_1_overflow), .in13(undriven_7), .in14(undriven_8),
    .in15(undriven_8), .out(ZCNO), .sel(FunSel));
  Multiplexer #(.select(4), .width(8), .enable("false")) multiplexer_2 (
    .in0(A), .in1(B), .in2(not_2_out), .in3(not_3_out), .in4(arithmeticunit_1_out),
    .in5(arithmeticunit_1_out), .in6(arithmeticunit_1_out), .in7(logicunit_1_out), .in8(logicunit_1_out),
    .in9(logicunit_1_out), .in10(logicalshift_1_out), .in11(logicalshift_1_out),
    .in12(arithmeticleftshift_1_out), .in13(arithmeticrightshift_1_out), .in14(circularshift_1_out),
    .in15(circularshift_1_out), .out(Output), .sel(FunSel));
  Hex_Digit_Display hex_digit_display_5 (.value(Output[7:4]));  // open: dp
  Hex_Digit_Display hex_digit_display_6 (.value(Output[3:0]));  // open: dp
endmodule

module ArithmeticUnit (
  input  Cin,
  input  [1:0] SEL,
  input  [7:0] A,
  input  [7:0] B,
  output [7:0] Out,
  output Zero,
  output Negative,
  output Overflow,
  output Carry
);

  wire adder_1_cout, adder_2_cout, adder_3_cout, adder_4_cout, adder_5_cout, adder_6_cout, adder_7_cout,
       multiplexer_1_out, xor_1_out, xor_2_out, xor_3_out, xor_4_out, xor_5_out, xor_6_out, xor_7_out,
       xor_8_out;

  Multiplexer #(.select(2), .enable("false")) multiplexer_1 (
    .in0(1'b0), .in1(Cin), .in2(1'b1), .out(multiplexer_1_out), .sel(SEL));  // open: in3
  xor xor_1 (xor_1_out, SEL[1], B[0]);
  xor xor_2 (xor_2_out, SEL[1], B[1]);
  xor xor_3 (xor_3_out, SEL[1], B[2]);
  xor xor_4 (xor_4_out, SEL[1], B[3]);
  xor xor_5 (xor_5_out, SEL[1], B[4]);
  xor xor_6 (xor_6_out, SEL[1], B[5]);
  xor xor_7 (xor_7_out, SEL[1], B[6]);
  xor xor_8 (xor_8_out, SEL[1], B[7]);
  Adder #(.width(1)) adder_1 (.a(A[0]), .b(xor_1_out), .out(Out[0]), .cin(multiplexer_1_out), .cout(adder_1_cout));
  Adder #(.width(1)) adder_2 (.a(A[1]), .b(xor_2_out), .out(Out[1]), .cin(adder_1_cout), .cout(adder_2_cout));
  Adder #(.width(1)) adder_3 (.a(A[2]), .b(xor_3_out), .out(Out[2]), .cin(adder_2_cout), .cout(adder_3_cout));
  Adder #(.width(1)) adder_4 (.a(A[3]), .b(xor_4_out), .out(Out[3]), .cin(adder_3_cout), .cout(adder_4_cout));
  Adder #(.width(1)) adder_5 (.a(A[4]), .b(xor_5_out), .out(Out[4]), .cin(adder_4_cout), .cout(adder_5_cout));
  Adder #(.width(1)) adder_6 (.a(A[5]), .b(xor_6_out), .out(Out[5]), .cin(adder_5_cout), .cout(adder_6_cout));
  Adder #(.width(1)) adder_7 (.a(A[6]), .b(xor_7_out), .out(Out[6]), .cin(adder_6_cout), .cout(adder_7_cout));
  Adder #(.width(1)) adder_8 (.a(A[7]), .b(xor_8_out), .out(Negative), .cin(adder_7_cout), .cout(Carry));
  xor xor_9 (Overflow, adder_7_cout, Carry);
  ZeroDetector zerodetector_1 (.In({Negative, Out[6:0]}), .Zero(Zero));

  assign Out[7] = Negative;
endmodule

module ZeroDetector (
  input  [7:0] In,
  output Zero
);

  wire or_1_out;

  or or_1 (or_1_out, In[0], In[1], In[2], In[3], In[4], In[5], In[6], In[7]);
  not not_1 (Zero, or_1_out);
endmodule

module LogicalShift (
  input  LR,
  input  [7:0] A,
  output [7:0] Out,
  output Zero,
  output Negative,
  output Carry
);

  Multiplexer #(.enable("false")) multiplexer_1 (.in0(1'b0), .in1(A[1]), .out(Out[0]), .sel(LR));
  Multiplexer #(.enable("false")) multiplexer_2 (.in0(A[0]), .in1(A[2]), .out(Out[1]), .sel(LR));
  Multiplexer #(.enable("false")) multiplexer_3 (.in0(A[1]), .in1(A[3]), .out(Out[2]), .sel(LR));
  Multiplexer #(.enable("false")) multiplexer_4 (.in0(A[2]), .in1(A[4]), .out(Out[3]), .sel(LR));
  Multiplexer #(.enable("false")) multiplexer_5 (.in0(A[3]), .in1(A[5]), .out(Out[4]), .sel(LR));
  Multiplexer #(.enable("false")) multiplexer_6 (.in0(A[4]), .in1(A[6]), .out(Out[5]), .sel(LR));
  Multiplexer #(.enable("false")) multiplexer_7 (.in0(A[5]), .in1(A[7]), .out(Out[6]), .sel(LR));
  Multiplexer #(.enable("false")) multiplexer_8 (.in0(A[6]), .in1(1'b0), .out(Negative), .sel(LR));
  ZeroDetector zerodetector_1 (.In({Negative, Out[6:0]}), .Zero(Zero));
  Multiplexer #(.enable("false")) multiplexer_9 (.in0(A[7]), .in1(A[0]), .out(Carry), .sel(LR));

  assign Out[7] = Negative;
endmodule

module LogicUnit (
  input  [7:0] A,
  input  [7:0] B,
  input  [1:0] SEL,
  output [7:0] Out,
  output Zero,
  output Negative
);

  wire [7:0] and_1_out, or_1_out, xor_1_out;

  assign or_1_out = A | B;  // OR_Gate or_1, 8 bits wide
  assign xor_1_out = A ^ B;  // XOR_Gate xor_1, 8 bits wide
  assign and_1_out = A & B;  // AND_Gate and_1, 8 bits wide
  Multiplexer #(.select(2), .width(8), .enable("false")) multiplexer_1 (
    .in0(or_1_out), .in1(xor_1_out), .in3(and_1_out), .out({Negative, Out[6:0]}), .sel(SEL));  // open: in2
  ZeroDetector zerodetector_1 (.In({Negative, Out[6:0]}), .Zero(Zero));

  assign Out[7] = Negative;
endmodule

module CircularShift (
  input  LR,
  input  [7:0] A,
  output [7:0] Out,
  output Zero,
  output Negative,
  output Carry
);

  Multiplexer #(.enable("false")) multiplexer_1 (.in0(A[7]), .in1(A[1]), .out(Out[0]), .sel(LR));
  Multiplexer #(.enable("false")) multiplexer_2 (.in0(A[0]), .in1(A[2]), .out(Out[1]), .sel(LR));
  Multiplexer #(.enable("false")) multiplexer_3 (.in0(A[1]), .in1(A[3]), .out(Out[2]), .sel(LR));
  Multiplexer #(.enable("false")) multiplexer_4 (.in0(A[2]), .in1(A[4]), .out(Out[3]), .sel(LR));
  Multiplexer #(.enable("false")) multiplexer_5 (.in0(A[3]), .in1(A[5]), .out(Out[4]), .sel(LR));
  Multiplexer #(.enable("false")) multiplexer_6 (.in0(A[4]), .in1(A[6]), .out(Out[5]), .sel(LR));
  Multiplexer #(.enable("false")) multiplexer_7 (.in0(A[5]), .in1(A[7]), .out(Out[6]), .sel(LR));
  Multiplexer #(.enable("false")) multiplexer_8 (.in0(A[6]), .in1(A[0]), .out(Negative), .sel(LR));
  ZeroDetector zerodetector_1 (.In({Negative, Out[6:0]}), .Zero(Zero));
  Multiplexer #(.enable("false")) multiplexer_9 (.in0(A[7]), .in1(A[0]), .out(Carry), .sel(LR));

  assign Out[7] = Negative;
endmodule

module ArithmeticRightShift (
  input  [7:0] A,
  output [7:0] Out,
  output Zero
);

  ZeroDetector zerodetector_1 (.In({{2{A[7]}}, A[6:1]}), .Zero(Zero));

  assign Out = {{2{A[7]}}, A[6:1]};
endmodule

module ArithmeticLeftShift (
  input  [7:0] A,
  output [7:0] Out,
  output Zero,
  output Negative,
  output Overflow
);

  ZeroDetector zerodetector_1 (.In({A[6:0], 1'b0}), .Zero(Zero));
  xor xor_1 (Overflow, A[6], A[7]);

  assign Negative = A[6];
  assign Out = {A[6:0], 1'b0};
endmodule

module ZCNO (
  input  CLK,
  input  [3:0] ZCNO_IN,
  output [3:0] ZCNO_OUT
);

  D_Flip_Flop Z (.clk(CLK), .D(ZCNO_IN[3]), .Q(ZCNO_OUT[3]));  // open: Qn, preset, en, reset
  D_Flip_Flop C (.clk(CLK), .D(ZCNO_IN[2]), .Q(ZCNO_OUT[2]));  // open: Qn, preset, en, reset
  D_Flip_Flop N (.clk(CLK), .D(ZCNO_IN[1]), .Q(ZCNO_OUT[1]));  // open: Qn, preset, en, reset
  D_Flip_Flop O (.clk(CLK), .D(ZCNO_IN[0]), .Q(ZCNO_OUT[0]));  // open: Qn, preset, en, reset
endmodule
