// Logisim project WholeSystem(Part4).circ as structural Verilog: 1 circuit, main circuit main
module main (
  input  CLOCK,
  input  [3:0] FunSel,
  input  [2:0] OutASel,
  input  [2:0] OutBSel,
  input  [1:0] FunSel_2,
  input  [3:0] RegSel,
  input  [3:0] TmpSel,
  input  [1:0] MUXASel,
  input  [1:0] MUXBSel,
  input  [1:0] OutCSel,
  input  [1:0] OutDSel,
  input  in_12,
  input  in_13,
  input  in_14,
  input  in_15,
  input  [1:0] FunSel_3,
  input  [2:0] RegSel_2,
  input  L_H,
  input  [1:0] FunSel_4,
  input  Enable,
  output [3:0] ZCNO,
  output [7:0] IR_8_15
);

  wire [3:0] ALU_zcno;
  wire [7:0] Adress_Register_File_outc, Adress_Register_File_outd, ALU_output, Instruction_Register_irout,
       multiplexer_1_out, multiplexer_2_out, ram_1_data, Register_File_outa, Register_File_outb;

  Multiplexer #(.select(2), .width(8), .enable("false")) multiplexer_1 (
    .in0(ALU_output), .in1(ram_1_data), .in2(Instruction_Register_irout), .in3(Adress_Register_File_outc),
    .out(multiplexer_1_out), .sel(MUXASel));
  _16_bit_InstructionRegister_Part1b__main Instruction_Register (
    .FunSel(FunSel_4), .L_nH(L_H), .I(ram_1_data), .E(Enable), .CLK(CLOCK),
    .IRout({IR_8_15, Instruction_Register_irout}));
  Multiplexer #(.select(2), .width(8), .enable("false")) multiplexer_2 (
    .in0(ALU_output), .in1(ram_1_data), .in2(Instruction_Register_irout), .in3(Adress_Register_File_outc),
    .out(multiplexer_2_out), .sel(MUXBSel));
  _8_bit_GeneralRegisterFile_Part2a__main Register_File (
    .RegSel(RegSel), .CLK(CLOCK), .FunSel(FunSel_2), .Input(multiplexer_1_out), .OutASel(OutASel),
    .OutBSel(OutBSel), .TempSel(TmpSel), .OutA(Register_File_outa), .OutB(Register_File_outb));
  _8_bit_AdressRegisterFile_Part2b__main Adress_Register_File (
    .RegSel(RegSel_2), .Input(multiplexer_2_out), .OutCSel(OutCSel), .FunSel(FunSel_3), .OutDSel(OutDSel),
    .CLK(CLOCK), .OutC(Adress_Register_File_outc), .OutD(Adress_Register_File_outd));
  Hex_Digit_Display hex_digit_display_1 (.value(IR_8_15[7:4]));  // open: dp
  Hex_Digit_Display hex_digit_display_2 (.value(IR_8_15[3:0]));  // open: dp
  ALU ALU (
    .A(Register_File_outa), .B(Register_File_outb), .Cin(ZCNO[2]), .ZCNO(ALU_zcno), .Output(ALU_output),
    .FunSel(FunSel));
  ZCNO zcno_1 (.ZCNO_IN(ALU_zcno), .CLK(CLOCK), .ZCNO_OUT(ZCNO));
  RAM #(.bus("separate")) ram_1 (
    .addr(Adress_Register_File_outd), .din(ALU_output), .data(ram_1_data), .str(in_12), .sel(in_13),
    .clk(CLOCK), .ld(in_14), .clr(in_15));
endmodule
