// Logisim project 16-bit_Adder_subtractor.circ as structural Verilog: 1 circuit, main circuit main
module main (
  input  Adder_Subtractor,
  input  [15:0] B,
  input  [15:0] A,
  output [15:0] O,
  output Cout
);

  wire [15:0] xor_1_out;

  Hex_Digit_Display hex_digit_display_1 (.value(B[15:12]));  // open: dp
  Hex_Digit_Display hex_digit_display_2 (.value(B[11:8]));  // open: dp
  Hex_Digit_Display hex_digit_display_3 (.value(A[11:8]));  // open: dp
  Hex_Digit_Display hex_digit_display_4 (.value(A[15:12]));  // open: dp
  Hex_Digit_Display hex_digit_display_5 (.value(B[3:0]));  // open: dp
  Hex_Digit_Display hex_digit_display_6 (.value(B[7:4]));  // open: dp
  Hex_Digit_Display hex_digit_display_7 (.value(A[7:4]));  // open: dp
  Hex_Digit_Display hex_digit_display_8 (.value(A[3:0]));  // open: dp
  assign xor_1_out = {16{Adder_Subtractor}} ^ B;  // XOR_Gate xor_1, 16 bits wide
  Adder #(.width(16)) adder_1 (.a(xor_1_out), .b(A), .out(O), .cin(Adder_Subtractor), .cout(Cout));
  Hex_Digit_Display hex_digit_display_9 (.value(O[15:12]));  // open: dp
  Hex_Digit_Display hex_digit_display_10 (.value(O[11:8]));  // open: dp
  Hex_Digit_Display hex_digit_display_11 (.value(O[3:0]));  // open: dp
  Hex_Digit_Display hex_digit_display_12 (.value(O[7:4]));  // open: dp
endmodule
