// Logisim project 16-bit_InstructionRegister(Part1b).circ as structural Verilog: 1 circuit, main circuit main
module main (
  input  E,
  input  CLK,
  input  [1:0] FunSel,
  input  L_nH,
  input  [7:0] I,
  output [15:0] IRout
);

  wire not_1_out;
  wire [7:0] multiplexer_1_out, multiplexer_2_out;
  wire [15:0] Adder_Subtractor_o, multiplexer_3_out;

  Hex_Digit_Display hex_digit_display_1 (.value(I[3:0]));  // open: dp
  Hex_Digit_Display hex_digit_display_2 (.value(I[7:4]));  // open: dp
  not not_1 (not_1_out, FunSel[0]);
  Multiplexer #(.width(8), .enable("false")) multiplexer_1 (
    .in0(IRout[7:0]), .in1(I), .out(multiplexer_1_out), .sel(L_nH));
  Multiplexer #(.width(8), .enable("false")) multiplexer_2 (
    .in0(I), .in1(IRout[15:8]), .out(multiplexer_2_out), .sel(L_nH));
  _16_bit_Adder_subtractor_main Adder_Subtractor (
    .Adder_Subtractor(not_1_out), .B(16'h1), .A(IRout), .O(Adder_Subtractor_o));  // open: Cout
  Multiplexer #(.select(2), .width(16)) multiplexer_3 (
    .in0(Adder_Subtractor_o), .in1(Adder_Subtractor_o), .in2({multiplexer_2_out, multiplexer_1_out}),
    .in3({16{1'b0}}), .out(multiplexer_3_out), .sel(FunSel), .en(E));
  _16_bit_D_FlipFlop_main _16_bit_D_FF (.I(multiplexer_3_out), .E(E), .CLK(CLK), .O(IRout));
  Hex_Digit_Display hex_digit_display_3 (.value(IRout[11:8]));  // open: dp
  Hex_Digit_Display hex_digit_display_4 (.value(IRout[15:12]));  // open: dp
  Hex_Digit_Display hex_digit_display_5 (.value(IRout[7:4]));  // open: dp
  Hex_Digit_Display hex_digit_display_6 (.value(IRout[3:0]));  // open: dp
endmodule
