// Logisim project 8-bit_AdressRegisterFile(Part2b).circ as structural Verilog: 1 circuit, main circuit main
module main (
  input  CLK,
  input  [2:0] RegSel,
  input  [7:0] Input,
  input  [1:0] OutCSel,
  input  [1:0] FunSel,
  input  [1:0] OutDSel,
  output [7:0] OutC,
  output [7:0] OutD
);

  wire not_1_out, not_2_out, not_3_out;
  wire [7:0] AR_q, PC_q, SP_q;

  Hex_Digit_Display hex_digit_display_1 (.value(Input[7:4]));  // open: dp
  Hex_Digit_Display hex_digit_display_2 (.value(Input[3:0]));  // open: dp
  not not_1 (not_1_out, RegSel[0]);
  not not_2 (not_2_out, RegSel[1]);
  not not_3 (not_3_out, RegSel[2]);
  _8_bit_Register_Part1a__main PC (.FunSel(FunSel), .I(Input), .E(not_3_out), .CLK(CLK), .Q(PC_q));
  _8_bit_Register_Part1a__main AR (.FunSel(FunSel), .I(Input), .E(not_2_out), .CLK(CLK), .Q(AR_q));
  _8_bit_Register_Part1a__main SP (.FunSel(FunSel), .I(Input), .E(not_1_out), .CLK(CLK), .Q(SP_q));
  Multiplexer #(.select(2), .width(8), .enable("false")) multiplexer_1 (
    .in0(PC_q), .in1(PC_q), .in2(AR_q), .in3(SP_q), .out(OutC), .sel(OutCSel));
  Multiplexer #(.select(2), .width(8), .enable("false")) multiplexer_2 (
    .in0(PC_q), .in1(PC_q), .in2(AR_q), .in3(SP_q), .out(OutD), .sel(OutDSel));
  Hex_Digit_Display hex_digit_display_3 (.value(OutC[7:4]));  // open: dp
  Hex_Digit_Display hex_digit_display_4 (.value(OutD[7:4]));  // open: dp
  Hex_Digit_Display hex_digit_display_5 (.value(OutC[3:0]));  // open: dp
  Hex_Digit_Display hex_digit_display_6 (.value(OutD[3:0]));  // open: dp
endmodule
