// Logisim project 8-bit_D-FlipFlop.circ as structural Verilog: 1 circuit, main circuit main
module main (
  input  E,
  input  CLK,
  input  [7:0] I,
  output [7:0] O
);

  Hex_Digit_Display hex_digit_display_1 (.value(I[7:4]));  // open: dp
  Hex_Digit_Display hex_digit_display_2 (.value(I[3:0]));  // open: dp
  D_Flip_Flop d_ff_1 (.clk(CLK), .D(I[0]), .Q(O[0]), .en(E));  // open: Qn, preset, reset
  D_Flip_Flop d_ff_2 (.clk(CLK), .D(I[1]), .Q(O[1]), .en(E));  // open: Qn, preset, reset
  D_Flip_Flop d_ff_3 (.clk(CLK), .D(I[2]), .Q(O[2]), .en(E));  // open: Qn, preset, reset
  D_Flip_Flop d_ff_4 (.clk(CLK), .D(I[3]), .Q(O[3]), .en(E));  // open: Qn, preset, reset
  D_Flip_Flop d_ff_5 (.clk(CLK), .D(I[4]), .Q(O[4]), .en(E));  // open: Qn, preset, reset
  D_Flip_Flop d_ff_6 (.clk(CLK), .D(I[5]), .Q(O[5]), .en(E));  // open: Qn, preset, reset
  D_Flip_Flop d_ff_7 (.clk(CLK), .D(I[6]), .Q(O[6]), .en(E));  // open: Qn, preset, reset
  D_Flip_Flop d_ff_8 (.clk(CLK), .D(I[7]), .Q(O[7]), .en(E));  // open: Qn, preset, reset
  Hex_Digit_Display hex_digit_display_3 (.value(O[7:4]));  // open: dp
  Hex_Digit_Display hex_digit_display_4 (.value(O[3:0]));  // open: dp
endmodule
