// Logisim project HWcontrolUnitProject2.circ as structural Verilog: 2 circuits, main circuit main
module main (
);

  wire ADD, AddressingMode, AND, and_1_out, and_2_out, and_3_out, and_4_out, and_5_out, and_6_out, and_7_out,
       and_8_out, and_9_out, and_10_out, and_11_out, and_12_out, and_13_out, and_14_out, and_15_out,
       and_16_out, and_17_out, and_18_out, and_19_out, and_20_out, and_21_out, and_22_out, and_23_out,
       and_24_out, and_25_out, and_26_out, and_27_out, and_28_out, and_29_out, and_30_out, and_31_out,
       and_32_out, and_33_out, and_34_out, and_35_out, and_36_out, and_37_out, BNE, BRA, C, clock_1_out, DEC,
       INC, IREnable, L_H, LD, LSL, LSR, MemLd, MemSel, MemStr, MOV, N, NOT, not_1_out, not_2_out, not_3_out,
       not_4_out, not_5_out, not_6_out, not_7_out, not_8_out, not_9_out, not_10_out, not_11_out, not_12_out,
       not_14_out, not_15_out, not_16_out, not_17_out, not_18_out, not_19_out, not_20_out, not_21_out,
       not_22_out, not_26_out, not_27_out, not_29_out, not_31_out, not_32_out, not_33_out, not_34_out,
       not_35_out, O, OR, or_1_out, or_2_out, or_3_out, or_4_out, or_5_out, or_6_out, or_7_out, or_8_out,
       or_9_out, or_10_out, or_11_out, or_12_out, or_13_out, or_14_out, or_15_out, or_16_out, or_17_out,
       or_18_out, or_19_out, or_20_out, or_21_out, or_22_out, or_23_out, or_24_out, or_25_out, PSH, PUL,
       Reset, ST, SUB, T0, T1, T2, T3, T4, T5, T6, T7, TempFlagDest, TempFlagSrc1, TempFlagSrc2, Z;
  wire [1:0] AddressFunSel, IRFunSel, MUXASel, MUXBSel, OutCSel, OutDSel, RegFileFunSel;
  wire [2:0] AddressRegSel, multiplexer_1_out, multiplexer_2_out, multiplexer_4_out, multiplexer_8_out,
       multiplexer_12_out, multiplexer_13_out, multiplexer_14_out, multiplexer_16_out, multiplexer_19_out,
       multiplexer_21_out, OutASel, OutBSel;
  wire [3:0] ALUFunSel, DecodedALUFunSel, decoder_1_out3, decoder_3_out3, decoder_4_out3, DestReg,
       multiplexer_3_out, multiplexer_5_out, multiplexer_6_out, multiplexer_7_out, multiplexer_9_out,
       multiplexer_10_out, multiplexer_11_out, multiplexer_17_out, multiplexer_18_out, multiplexer_20_out,
       not_13_out, not_28_out, not_30_out, RegFileRegSel, RegFileTmpSel;
  wire [7:0] Address;
  wire [15:12] Instruction;

  or or_1 (or_1_out, NOT, LSR, LSL);
  Multiplexer #(.select(2), .width(3), .enable("false")) multiplexer_1 (
    .in0(3'b011), .in1(3'b011), .in2(3'b101), .in3(3'b110), .out(multiplexer_1_out), .sel(DestReg[1:0]));
  or or_2 (or_2_out, AND, OR, ADD, SUB);
  and and_1 (and_1_out, BRA, AddressingMode, T2);
  not not_1 (not_1_out, AddressingMode);
  and and_2 (and_2_out, BRA, not_1_out, T2);
  Multiplexer #(.select(2), .width(3), .enable("false")) multiplexer_2 (
    .in0(3'b011), .in1(3'b011), .in2(3'b101), .in3(3'b110), .out(multiplexer_2_out), .sel(DestReg[1:0]));
  or or_3 (or_3_out, INC, DEC);
  Multiplexer #(.select(2), .width(4), .enable("false")) multiplexer_3 (
    .in0(4'b0111), .in1(4'b1011), .in2(4'b1101), .in3(4'b1110), .out(multiplexer_3_out), .sel(DestReg[1:0]));
  Multiplexer #(.select(2), .width(3), .enable("false")) multiplexer_4 (
    .in0(3'b011), .in1(3'b011), .in2(3'b101), .in3(3'b110), .out(multiplexer_4_out), .sel(DestReg[1:0]));
  or or_4 (or_4_out, and_1_out, and_6_out);
  assign MUXBSel = or_4_out ? 2'b10 : 2'bz;  // Controlled_Buffer controlled_buffer_1
  assign AddressRegSel = or_4_out ? 3'b011 : 3'bz;  // Controlled_Buffer controlled_buffer_2
  assign AddressFunSel = or_4_out ? 2'b10 : 2'bz;  // Controlled_Buffer controlled_buffer_3
  assign MemSel = or_4_out ? 1'b1 : 1'bz;  // Controlled_Buffer controlled_buffer_4
  assign MemStr = or_4_out ? 1'b0 : 1'bz;  // Controlled_Buffer controlled_buffer_5
  assign MemLd = or_4_out ? 1'b0 : 1'bz;  // Controlled_Buffer controlled_buffer_6
  assign Reset = or_4_out ? 1'b1 : 1'bz;  // Controlled_Buffer controlled_buffer_7
  assign IREnable = or_4_out ? 1'b0 : 1'bz;  // Controlled_Buffer controlled_buffer_8
  assign RegFileRegSel = or_4_out ? 4'b1111 : 4'bz;  // Controlled_Buffer controlled_buffer_9
  assign RegFileTmpSel = or_4_out ? 4'b1111 : 4'bz;  // Controlled_Buffer controlled_buffer_10
  or or_5 (or_5_out, not_1_out, Z);
  or or_6 (or_6_out, and_2_out, and_7_out);
  assign Reset = or_6_out ? 1'b1 : 1'bz;  // Controlled_Buffer controlled_buffer_11
  and and_3 (and_3_out, TempFlagSrc1, MOV, T2, TempFlagDest);
  assign MUXBSel = and_3_out ? 2'b11 : 2'bz;  // Controlled_Buffer controlled_buffer_12
  assign OutCSel = and_3_out ? Address[5:4] : 2'bz;  // Controlled_Buffer controlled_buffer_13
  assign MemSel = and_3_out ? 1'b1 : 1'bz;  // Controlled_Buffer controlled_buffer_14
  assign MemStr = and_3_out ? 1'b0 : 1'bz;  // Controlled_Buffer controlled_buffer_15
  assign MemLd = and_3_out ? 1'b0 : 1'bz;  // Controlled_Buffer controlled_buffer_16
  assign AddressRegSel = and_3_out ? multiplexer_2_out : 3'bz;  // Controlled_Buffer controlled_buffer_17
  assign Reset = and_3_out ? 1'b1 : 1'bz;  // Controlled_Buffer controlled_buffer_18
  assign IREnable = and_3_out ? 1'b0 : 1'bz;  // Controlled_Buffer controlled_buffer_19
  assign RegFileRegSel = and_3_out ? 4'b1111 : 4'bz;  // Controlled_Buffer controlled_buffer_20
  assign RegFileTmpSel = and_3_out ? 4'b1111 : 4'bz;  // Controlled_Buffer controlled_buffer_21
  assign AddressFunSel = and_3_out ? 2'b10 : 2'bz;  // Controlled_Buffer controlled_buffer_22
  and and_4 (and_4_out, TempFlagSrc1, or_1_out, T3, TempFlagDest);
  assign MUXBSel = and_4_out ? 2'b00 : 2'bz;  // Controlled_Buffer controlled_buffer_23
  assign OutASel = and_4_out ? 3'b100 : 3'bz;  // Controlled_Buffer controlled_buffer_24
  assign MemSel = and_4_out ? 1'b1 : 1'bz;  // Controlled_Buffer controlled_buffer_25
  assign MemStr = and_4_out ? 1'b0 : 1'bz;  // Controlled_Buffer controlled_buffer_26
  assign MemLd = and_4_out ? 1'b0 : 1'bz;  // Controlled_Buffer controlled_buffer_27
  assign AddressRegSel = and_4_out ? multiplexer_1_out : 3'bz;  // Controlled_Buffer controlled_buffer_28
  assign Reset = and_4_out ? 1'b1 : 1'bz;  // Controlled_Buffer controlled_buffer_29
  assign IREnable = and_4_out ? 1'b0 : 1'bz;  // Controlled_Buffer controlled_buffer_30
  assign RegFileRegSel = and_4_out ? 4'b1111 : 4'bz;  // Controlled_Buffer controlled_buffer_31
  assign RegFileTmpSel = and_4_out ? 4'b1111 : 4'bz;  // Controlled_Buffer controlled_buffer_32
  assign AddressFunSel = and_4_out ? 2'b10 : 2'bz;  // Controlled_Buffer controlled_buffer_33
  assign ALUFunSel = and_4_out ? DecodedALUFunSel : 4'bz;  // Controlled_Buffer controlled_buffer_34
  not not_2 (not_2_out, TempFlagSrc1);
  not not_3 (not_3_out, TempFlagSrc2);
  and and_5 (and_5_out, or_2_out, not_2_out, TempFlagDest, not_3_out, T2);
  assign MUXBSel = and_5_out ? 2'b00 : 2'bz;  // Controlled_Buffer controlled_buffer_35
  assign OutBSel = and_5_out ? {1'b0, Address[5:4]} : 3'bz;  // Controlled_Buffer controlled_buffer_36
  assign OutASel = and_5_out ? {1'b0, Address[1:0]} : 3'bz;  // Controlled_Buffer controlled_buffer_37
  assign MemSel = and_5_out ? 1'b1 : 1'bz;  // Controlled_Buffer controlled_buffer_38
  assign MemStr = and_5_out ? 1'b0 : 1'bz;  // Controlled_Buffer controlled_buffer_39
  assign MemLd = and_5_out ? 1'b0 : 1'bz;  // Controlled_Buffer controlled_buffer_40
  assign AddressRegSel = and_5_out ? multiplexer_4_out : 3'bz;  // Controlled_Buffer controlled_buffer_41
  assign Reset = and_5_out ? 1'b1 : 1'bz;  // Controlled_Buffer controlled_buffer_42
  assign IREnable = and_5_out ? 1'b0 : 1'bz;  // Controlled_Buffer controlled_buffer_43
  assign RegFileRegSel = and_5_out ? 4'b1111 : 4'bz;  // Controlled_Buffer controlled_buffer_44
  assign RegFileTmpSel = and_5_out ? 4'b1111 : 4'bz;  // Controlled_Buffer controlled_buffer_45
  assign AddressFunSel = and_5_out ? 2'b10 : 2'bz;  // Controlled_Buffer controlled_buffer_46
  assign ALUFunSel = and_5_out ? DecodedALUFunSel : 4'bz;  // Controlled_Buffer controlled_buffer_47
  WholeSystem_Part4__main main_1 (
    .ALUFunSel(ALUFunSel), .OutASel(OutASel), .OutBSel(OutBSel), .RegFileFunSel(RegFileFunSel),
    .RegFileRegSel(RegFileRegSel), .RegFileTmpSel(RegFileTmpSel), .MUXASel(MUXASel), .MUXBSel(MUXBSel),
    .OutCSel(OutCSel), .OutDSel(OutDSel), .AddressFunSel(AddressFunSel), .AddressRegSel(AddressRegSel),
    .L_H(L_H), .IRFunSel(IRFunSel), .IREnable(IREnable),
    .Instruction({Instruction, DestReg[3], AddressingMode, DestReg[1:0], Address}), .MemStr(MemStr),
    .MemSel(MemSel), .ZCNO({Z, C, N, O}), .MemLd(MemLd), .CLK(clock_1_out));  // open: MemClr
  not not_4 (not_4_out, Z);
  and and_6 (and_6_out, AddressingMode, T2, not_4_out, BNE);
  and and_7 (and_7_out, or_5_out, T2, BNE);
  or or_7 (or_7_out, NOT, LSR, LSL);
  not not_5 (not_5_out, TempFlagDest);
  not not_6 (not_6_out, TempFlagSrc1);
  and and_8 (and_8_out, or_3_out, not_6_out, not_5_out, T3);
  assign MUXASel = and_8_out ? 2'b00 : 2'bz;  // Controlled_Buffer controlled_buffer_48
  assign OutASel = and_8_out ? {1'b0, Address[5:4]} : 3'bz;  // Controlled_Buffer controlled_buffer_49
  assign OutBSel = and_8_out ? 3'b111 : 3'bz;  // Controlled_Buffer controlled_buffer_50
  assign MemSel = and_8_out ? 1'b1 : 1'bz;  // Controlled_Buffer controlled_buffer_51
  assign MemStr = and_8_out ? 1'b0 : 1'bz;  // Controlled_Buffer controlled_buffer_52
  assign MemLd = and_8_out ? 1'b0 : 1'bz;  // Controlled_Buffer controlled_buffer_53
  assign AddressRegSel = and_8_out ? 3'b111 : 3'bz;  // Controlled_Buffer controlled_buffer_54
  assign Reset = and_8_out ? 1'b1 : 1'bz;  // Controlled_Buffer controlled_buffer_55
  assign IREnable = and_8_out ? 1'b0 : 1'bz;  // Controlled_Buffer controlled_buffer_56
  assign RegFileFunSel = and_8_out ? 2'b10 : 2'bz;  // Controlled_Buffer controlled_buffer_57
  assign RegFileTmpSel = and_8_out ? 4'b1111 : 4'bz;  // Controlled_Buffer controlled_buffer_58
  assign RegFileRegSel = and_8_out ? multiplexer_3_out : 4'bz;  // Controlled_Buffer controlled_buffer_59
  assign ALUFunSel = and_8_out ? DecodedALUFunSel : 4'bz;  // Controlled_Buffer controlled_buffer_60
  and and_9 (and_9_out, or_7_out, TempFlagSrc1, T2);
  Clock clock_1 (.out(clock_1_out));
  assign MUXASel = and_9_out ? 2'b11 : 2'bz;  // Controlled_Buffer controlled_buffer_61
  assign OutCSel = and_9_out ? Address[5:4] : 2'bz;  // Controlled_Buffer controlled_buffer_62
  assign MemSel = and_9_out ? 1'b1 : 1'bz;  // Controlled_Buffer controlled_buffer_63
  assign MemStr = and_9_out ? 1'b0 : 1'bz;  // Controlled_Buffer controlled_buffer_64
  assign MemLd = and_9_out ? 1'b0 : 1'bz;  // Controlled_Buffer controlled_buffer_65
  assign AddressRegSel = and_9_out ? 3'b111 : 3'bz;  // Controlled_Buffer controlled_buffer_66
  assign Reset = and_9_out ? 1'b0 : 1'bz;  // Controlled_Buffer controlled_buffer_67
  assign IREnable = and_9_out ? 1'b0 : 1'bz;  // Controlled_Buffer controlled_buffer_68
  assign RegFileRegSel = and_9_out ? 4'b1111 : 4'bz;  // Controlled_Buffer controlled_buffer_69
  assign RegFileTmpSel = and_9_out ? 4'b0111 : 4'bz;  // Controlled_Buffer controlled_buffer_70
  assign RegFileFunSel = and_9_out ? 2'b10 : 2'bz;  // Controlled_Buffer controlled_buffer_71
  Multiplexer #(.select(2), .width(4), .enable("false")) multiplexer_5 (
    .in0(4'b0111), .in1(4'b1011), .in2(4'b1101), .in3(4'b1110), .out(multiplexer_5_out), .sel(DestReg[1:0]));
  or or_8 (or_8_out, NOT, LSR, LSL);
  Multiplexer #(.select(2), .width(4), .enable("false")) multiplexer_6 (
    .in0(4'b0111), .in1(4'b1011), .in2(4'b1101), .in3(4'b1110), .out(multiplexer_6_out), .sel(DestReg[1:0]));
  or or_9 (or_9_out, AND, OR, ADD, SUB);
  Multiplexer #(.select(2), .width(4), .enable("false")) multiplexer_7 (
    .in0(4'b0111), .in1(4'b1011), .in2(4'b1101), .in3(4'b1110), .out(multiplexer_7_out), .sel(DestReg[1:0]));
  and and_10 (and_10_out, TempFlagSrc1, MOV, T2, not_7_out);
  assign MUXASel = and_10_out ? 2'b11 : 2'bz;  // Controlled_Buffer controlled_buffer_72
  assign OutCSel = and_10_out ? Address[5:4] : 2'bz;  // Controlled_Buffer controlled_buffer_73
  assign MemSel = and_10_out ? 1'b1 : 1'bz;  // Controlled_Buffer controlled_buffer_74
  assign MemStr = and_10_out ? 1'b0 : 1'bz;  // Controlled_Buffer controlled_buffer_75
  assign MemLd = and_10_out ? 1'b0 : 1'bz;  // Controlled_Buffer controlled_buffer_76
  assign AddressRegSel = and_10_out ? 3'b111 : 3'bz;  // Controlled_Buffer controlled_buffer_77
  assign Reset = and_10_out ? 1'b1 : 1'bz;  // Controlled_Buffer controlled_buffer_78
  assign IREnable = and_10_out ? 1'b0 : 1'bz;  // Controlled_Buffer controlled_buffer_79
  assign RegFileRegSel = and_10_out ? multiplexer_5_out : 4'bz;  // Controlled_Buffer controlled_buffer_80
  assign RegFileTmpSel = and_10_out ? 4'b1111 : 4'bz;  // Controlled_Buffer controlled_buffer_81
  assign RegFileFunSel = and_10_out ? 2'b10 : 2'bz;  // Controlled_Buffer controlled_buffer_82
  or or_10 (or_10_out, INC, DEC);
  SequentialCounter Sequential_Counter (
    .T0(T0), .T1(T1), .T2(T2), .T3(T3), .T4(T4), .T5(T5), .T6(T6), .T7(T7), .CLK(clock_1_out), .Reset(Reset));
  not not_7 (not_7_out, TempFlagDest);
  and and_11 (and_11_out, TempFlagSrc1, or_8_out, T3, not_11_out);
  assign MUXASel = and_11_out ? 2'b00 : 2'bz;  // Controlled_Buffer controlled_buffer_83
  assign OutASel = and_11_out ? 3'b100 : 3'bz;  // Controlled_Buffer controlled_buffer_84
  assign MemSel = and_11_out ? 1'b1 : 1'bz;  // Controlled_Buffer controlled_buffer_85
  assign MemStr = and_11_out ? 1'b0 : 1'bz;  // Controlled_Buffer controlled_buffer_86
  assign MemLd = and_11_out ? 1'b0 : 1'bz;  // Controlled_Buffer controlled_buffer_87
  assign AddressRegSel = and_11_out ? 3'b111 : 3'bz;  // Controlled_Buffer controlled_buffer_88
  assign Reset = and_11_out ? 1'b1 : 1'bz;  // Controlled_Buffer controlled_buffer_89
  assign IREnable = and_11_out ? 1'b0 : 1'bz;  // Controlled_Buffer controlled_buffer_90
  assign RegFileRegSel = and_11_out ? multiplexer_6_out : 4'bz;  // Controlled_Buffer controlled_buffer_91
  assign RegFileTmpSel = and_11_out ? 4'b1111 : 4'bz;  // Controlled_Buffer controlled_buffer_92
  assign RegFileFunSel = and_11_out ? 2'b10 : 2'bz;  // Controlled_Buffer controlled_buffer_93
  assign ALUFunSel = and_11_out ? DecodedALUFunSel : 4'bz;  // Controlled_Buffer controlled_buffer_94
  Multiplexer #(.select(2), .width(3), .enable("false")) multiplexer_8 (
    .in0(3'b011), .in1(3'b011), .in2(3'b101), .in3(3'b110), .out(multiplexer_8_out), .sel(DestReg[1:0]));
  not not_8 (not_8_out, TempFlagDest);
  not not_9 (not_9_out, TempFlagSrc1);
  not not_10 (not_10_out, TempFlagSrc2);
  and and_12 (and_12_out, or_9_out, not_9_out, not_8_out, not_10_out, T2);
  assign MUXASel = and_12_out ? 2'b00 : 2'bz;  // Controlled_Buffer controlled_buffer_95
  assign OutBSel = and_12_out ? {1'b0, Address[5:4]} : 3'bz;  // Controlled_Buffer controlled_buffer_96
  assign OutASel = and_12_out ? {1'b0, Address[1:0]} : 3'bz;  // Controlled_Buffer controlled_buffer_97
  assign MemSel = and_12_out ? 1'b1 : 1'bz;  // Controlled_Buffer controlled_buffer_98
  assign MemStr = and_12_out ? 1'b0 : 1'bz;  // Controlled_Buffer controlled_buffer_99
  assign MemLd = and_12_out ? 1'b0 : 1'bz;  // Controlled_Buffer controlled_buffer_100
  assign AddressRegSel = and_12_out ? 3'b111 : 3'bz;  // Controlled_Buffer controlled_buffer_101
  assign Reset = and_12_out ? 1'b1 : 1'bz;  // Controlled_Buffer controlled_buffer_102
  assign IREnable = and_12_out ? 1'b0 : 1'bz;  // Controlled_Buffer controlled_buffer_103
  assign RegFileRegSel = and_12_out ? multiplexer_7_out : 4'bz;  // Controlled_Buffer controlled_buffer_104
  assign RegFileTmpSel = and_12_out ? 4'b1111 : 4'bz;  // Controlled_Buffer controlled_buffer_105
  assign RegFileFunSel = and_12_out ? 2'b10 : 2'bz;  // Controlled_Buffer controlled_buffer_106
  assign ALUFunSel = and_12_out ? DecodedALUFunSel : 4'bz;  // Controlled_Buffer controlled_buffer_107
  and and_13 (and_13_out, PSH, T2);
  assign OutASel = and_13_out ? {1'b0, DestReg[1:0]} : 3'bz;  // Controlled_Buffer controlled_buffer_108
  assign OutDSel = and_13_out ? 2'b11 : 2'bz;  // Controlled_Buffer controlled_buffer_109
  assign MemSel = and_13_out ? 1'b1 : 1'bz;  // Controlled_Buffer controlled_buffer_110
  assign MemStr = and_13_out ? 1'b1 : 1'bz;  // Controlled_Buffer controlled_buffer_111
  assign MemLd = and_13_out ? 1'b0 : 1'bz;  // Controlled_Buffer controlled_buffer_112
  assign AddressRegSel = and_13_out ? 3'b110 : 3'bz;  // Controlled_Buffer controlled_buffer_113
  assign Reset = and_13_out ? 1'b1 : 1'bz;  // Controlled_Buffer controlled_buffer_114
  assign IREnable = and_13_out ? 1'b0 : 1'bz;  // Controlled_Buffer controlled_buffer_115
  assign RegFileRegSel = and_13_out ? 4'b1111 : 4'bz;  // Controlled_Buffer controlled_buffer_116
  assign RegFileTmpSel = and_13_out ? 4'b1111 : 4'bz;  // Controlled_Buffer controlled_buffer_117
  assign ALUFunSel = and_13_out ? DecodedALUFunSel : 4'bz;  // Controlled_Buffer controlled_buffer_118
  assign AddressFunSel = and_13_out ? 2'b00 : 2'bz;  // Controlled_Buffer controlled_buffer_119
  not not_11 (not_11_out, TempFlagDest);
  not not_12 (not_12_out, TempFlagSrc1);
  and and_14 (and_14_out, or_10_out, not_12_out, TempFlagDest, T3);
  assign MUXBSel = and_14_out ? 2'b00 : 2'bz;  // Controlled_Buffer controlled_buffer_120
  assign OutASel = and_14_out ? {1'b0, Address[5:4]} : 3'bz;  // Controlled_Buffer controlled_buffer_121
  assign OutBSel = and_14_out ? 3'b111 : 3'bz;  // Controlled_Buffer controlled_buffer_122
  assign MemSel = and_14_out ? 1'b1 : 1'bz;  // Controlled_Buffer controlled_buffer_123
  assign MemStr = and_14_out ? 1'b0 : 1'bz;  // Controlled_Buffer controlled_buffer_124
  assign MemLd = and_14_out ? 1'b0 : 1'bz;  // Controlled_Buffer controlled_buffer_125
  assign AddressRegSel = and_14_out ? multiplexer_8_out : 3'bz;  // Controlled_Buffer controlled_buffer_126
  assign Reset = and_14_out ? 1'b1 : 1'bz;  // Controlled_Buffer controlled_buffer_127
  assign IREnable = and_14_out ? 1'b0 : 1'bz;  // Controlled_Buffer controlled_buffer_128
  assign AddressFunSel = and_14_out ? 2'b10 : 2'bz;  // Controlled_Buffer controlled_buffer_129
  assign RegFileTmpSel = and_14_out ? 4'b1111 : 4'bz;  // Controlled_Buffer controlled_buffer_130
  assign RegFileRegSel = and_14_out ? 4'b1111 : 4'bz;  // Controlled_Buffer controlled_buffer_131
  assign ALUFunSel = and_14_out ? DecodedALUFunSel : 4'bz;  // Controlled_Buffer controlled_buffer_132
  assign OutDSel = T0 ? 2'b00 : 2'bz;  // Controlled_Buffer controlled_buffer_133
  assign AddressRegSel = T0 ? 3'b011 : 3'bz;  // Controlled_Buffer controlled_buffer_134
  assign AddressFunSel = T0 ? 2'b01 : 2'bz;  // Controlled_Buffer controlled_buffer_135
  assign MemStr = T0 ? 1'b0 : 1'bz;  // Controlled_Buffer controlled_buffer_136
  assign MemSel = T0 ? 1'b1 : 1'bz;  // Controlled_Buffer controlled_buffer_137
  assign MemLd = T0 ? 1'b1 : 1'bz;  // Controlled_Buffer controlled_buffer_138
  assign IREnable = T0 ? 1'b1 : 1'bz;  // Controlled_Buffer controlled_buffer_139
  assign IRFunSel = T0 ? 2'b10 : 2'bz;  // Controlled_Buffer controlled_buffer_140
  assign L_H = T0 ? 1'b1 : 1'bz;  // Controlled_Buffer controlled_buffer_141
  assign RegFileRegSel = T0 ? 4'b1111 : 4'bz;  // Controlled_Buffer controlled_buffer_142
  assign RegFileTmpSel = T0 ? 4'b0000 : 4'bz;  // Controlled_Buffer controlled_buffer_143
  assign RegFileFunSel = T0 ? 2'b11 : 2'bz;  // Controlled_Buffer controlled_buffer_144
  assign Reset = T0 ? 1'b0 : 1'bz;  // Controlled_Buffer controlled_buffer_145
  Decoder #(.select(2), .enable("false")) decoder_1 (
    .out0(decoder_1_out3[3]), .out1(decoder_1_out3[2]), .out2(decoder_1_out3[1]), .out3(decoder_1_out3[0]),
    .sel(DestReg[1:0]));
  or or_11 (or_11_out, INC, DEC);
  assign OutDSel = T1 ? 2'b00 : 2'bz;  // Controlled_Buffer controlled_buffer_146
  assign AddressRegSel = T1 ? 3'b011 : 3'bz;  // Controlled_Buffer controlled_buffer_147
  assign AddressFunSel = T1 ? 2'b01 : 2'bz;  // Controlled_Buffer controlled_buffer_148
  assign MemStr = T1 ? 1'b0 : 1'bz;  // Controlled_Buffer controlled_buffer_149
  assign MemSel = T1 ? 1'b1 : 1'bz;  // Controlled_Buffer controlled_buffer_150
  assign MemLd = T1 ? 1'b1 : 1'bz;  // Controlled_Buffer controlled_buffer_151
  assign IREnable = T1 ? 1'b1 : 1'bz;  // Controlled_Buffer controlled_buffer_152
  assign IRFunSel = T1 ? 2'b10 : 2'bz;  // Controlled_Buffer controlled_buffer_153
  assign RegFileRegSel = T1 ? 4'b1111 : 4'bz;  // Controlled_Buffer controlled_buffer_154
  assign RegFileTmpSel = T1 ? 4'b1111 : 4'bz;  // Controlled_Buffer controlled_buffer_155
  assign L_H = T1 ? 1'b0 : 1'bz;  // Controlled_Buffer controlled_buffer_156
  assign Reset = T1 ? 1'b0 : 1'bz;  // Controlled_Buffer controlled_buffer_157
  and and_15 (and_15_out, PUL, T2);
  assign AddressRegSel = and_15_out ? 3'b110 : 3'bz;  // Controlled_Buffer controlled_buffer_158
  assign AddressFunSel = and_15_out ? 2'b01 : 2'bz;  // Controlled_Buffer controlled_buffer_159
  assign MemSel = and_15_out ? 1'b1 : 1'bz;  // Controlled_Buffer controlled_buffer_160
  assign MemStr = and_15_out ? 1'b0 : 1'bz;  // Controlled_Buffer controlled_buffer_161
  assign MemLd = and_15_out ? 1'b0 : 1'bz;  // Controlled_Buffer controlled_buffer_162
  assign Reset = and_15_out ? 1'b0 : 1'bz;  // Controlled_Buffer controlled_buffer_163
  assign IREnable = and_15_out ? 1'b0 : 1'bz;  // Controlled_Buffer controlled_buffer_164
  assign RegFileRegSel = and_15_out ? 4'b1111 : 4'bz;  // Controlled_Buffer controlled_buffer_165
  assign RegFileTmpSel = and_15_out ? 4'b1111 : 4'bz;  // Controlled_Buffer controlled_buffer_166
  assign not_13_out = ~decoder_1_out3;  // NOT_Gate not_13, 4 bits wide
  Multiplexer #(.select(2), .width(4), .enable("false")) multiplexer_9 (
    .in0(4'b0111), .in1(4'b1011), .in2(4'b1101), .in3(4'b1110), .out(multiplexer_9_out), .sel(DestReg[1:0]));
  or or_12 (or_12_out, NOT, LSR, LSL);
  Multiplexer #(.select(2), .width(4), .enable("false")) multiplexer_10 (
    .in0(4'b0111), .in1(4'b1011), .in2(4'b1101), .in3(4'b1110), .out(multiplexer_10_out), .sel(DestReg[1:0]));
  or or_13 (or_13_out, AND, OR, ADD, SUB);
  Multiplexer #(.select(2), .width(4), .enable("false")) multiplexer_11 (
    .in0(4'b0111), .in1(4'b1011), .in2(4'b1101), .in3(4'b1110), .out(multiplexer_11_out), .sel(DestReg[1:0]));
  and and_16 (and_16_out, PUL, T3);
  assign RegFileRegSel = and_16_out ? not_13_out : 4'bz;  // Controlled_Buffer controlled_buffer_167
  assign RegFileTmpSel = and_16_out ? 4'b1111 : 4'bz;  // Controlled_Buffer controlled_buffer_168
  assign RegFileFunSel = and_16_out ? 2'b10 : 2'bz;  // Controlled_Buffer controlled_buffer_169
  assign AddressRegSel = and_16_out ? 3'b111 : 3'bz;  // Controlled_Buffer controlled_buffer_170
  assign OutDSel = and_16_out ? 2'b11 : 2'bz;  // Controlled_Buffer controlled_buffer_171
  assign MemSel = and_16_out ? 1'b1 : 1'bz;  // Controlled_Buffer controlled_buffer_172
  assign MemStr = and_16_out ? 1'b0 : 1'bz;  // Controlled_Buffer controlled_buffer_173
  assign MemLd = and_16_out ? 1'b1 : 1'bz;  // Controlled_Buffer controlled_buffer_174
  assign MUXASel = and_16_out ? 2'b01 : 2'bz;  // Controlled_Buffer controlled_buffer_175
  assign Reset = and_16_out ? 1'b1 : 1'bz;  // Controlled_Buffer controlled_buffer_176
  assign IREnable = and_16_out ? 1'b0 : 1'bz;  // Controlled_Buffer controlled_buffer_177
  and and_17 (and_17_out, or_11_out, T2);
  assign MemSel = and_17_out ? 1'b1 : 1'bz;  // Controlled_Buffer controlled_buffer_178
  assign MemStr = and_17_out ? 1'b0 : 1'bz;  // Controlled_Buffer controlled_buffer_179
  assign MemLd = and_17_out ? 1'b0 : 1'bz;  // Controlled_Buffer controlled_buffer_180
  assign AddressRegSel = and_17_out ? 3'b111 : 3'bz;  // Controlled_Buffer controlled_buffer_181
  assign Reset = and_17_out ? 1'b0 : 1'bz;  // Controlled_Buffer controlled_buffer_182
  assign IREnable = and_17_out ? 1'b0 : 1'bz;  // Controlled_Buffer controlled_buffer_183
  assign RegFileRegSel = and_17_out ? 4'b1111 : 4'bz;  // Controlled_Buffer controlled_buffer_184
  assign RegFileTmpSel = and_17_out ? 4'b1110 : 4'bz;  // Controlled_Buffer controlled_buffer_185
  assign RegFileFunSel = and_17_out ? 2'b01 : 2'bz;  // Controlled_Buffer controlled_buffer_186
  or or_14 (or_14_out, INC, DEC);
  Multiplexer #(.select(2), .width(3), .enable("false")) multiplexer_12 (
    .in0(3'b011), .in1(3'b011), .in2(3'b101), .in3(3'b110), .out(multiplexer_12_out), .sel(DestReg[1:0]));
  not not_14 (not_14_out, TempFlagDest);
  not not_15 (not_15_out, TempFlagSrc1);
  and and_18 (and_18_out, MOV, not_15_out, not_14_out, T2);
  assign MUXASel = and_18_out ? 2'b00 : 2'bz;  // Controlled_Buffer controlled_buffer_187
  assign OutASel = and_18_out ? {1'b0, Address[5:4]} : 3'bz;  // Controlled_Buffer controlled_buffer_188
  assign MemSel = and_18_out ? 1'b1 : 1'bz;  // Controlled_Buffer controlled_buffer_189
  assign MemStr = and_18_out ? 1'b0 : 1'bz;  // Controlled_Buffer controlled_buffer_190
  assign MemLd = and_18_out ? 1'b0 : 1'bz;  // Controlled_Buffer controlled_buffer_191
  assign AddressRegSel = and_18_out ? 3'b111 : 3'bz;  // Controlled_Buffer controlled_buffer_192
  assign Reset = and_18_out ? 1'b1 : 1'bz;  // Controlled_Buffer controlled_buffer_193
  assign IREnable = and_18_out ? 1'b0 : 1'bz;  // Controlled_Buffer controlled_buffer_194
  assign RegFileRegSel = and_18_out ? multiplexer_9_out : 4'bz;  // Controlled_Buffer controlled_buffer_195
  assign RegFileTmpSel = and_18_out ? 4'b1111 : 4'bz;  // Controlled_Buffer controlled_buffer_196
  assign RegFileFunSel = and_18_out ? 2'b10 : 2'bz;  // Controlled_Buffer controlled_buffer_197
  assign ALUFunSel = and_18_out ? DecodedALUFunSel : 4'bz;  // Controlled_Buffer controlled_buffer_198
  not not_16 (not_16_out, TempFlagSrc1);
  not not_17 (not_17_out, TempFlagDest);
  and and_19 (and_19_out, or_12_out, not_16_out, not_17_out, T2);
  assign MUXASel = and_19_out ? 2'b00 : 2'bz;  // Controlled_Buffer controlled_buffer_199
  assign OutASel = and_19_out ? {1'b0, Address[5:4]} : 3'bz;  // Controlled_Buffer controlled_buffer_200
  assign MemSel = and_19_out ? 1'b1 : 1'bz;  // Controlled_Buffer controlled_buffer_201
  assign MemStr = and_19_out ? 1'b0 : 1'bz;  // Controlled_Buffer controlled_buffer_202
  assign MemLd = and_19_out ? 1'b0 : 1'bz;  // Controlled_Buffer controlled_buffer_203
  assign AddressRegSel = and_19_out ? 3'b111 : 3'bz;  // Controlled_Buffer controlled_buffer_204
  assign Reset = and_19_out ? 1'b1 : 1'bz;  // Controlled_Buffer controlled_buffer_205
  assign IREnable = and_19_out ? 1'b0 : 1'bz;  // Controlled_Buffer controlled_buffer_206
  assign RegFileRegSel = and_19_out ? multiplexer_10_out : 4'bz;  // Controlled_Buffer controlled_buffer_207
  assign RegFileTmpSel = and_19_out ? 4'b1111 : 4'bz;  // Controlled_Buffer controlled_buffer_208
  assign RegFileFunSel = and_19_out ? 2'b10 : 2'bz;  // Controlled_Buffer controlled_buffer_209
  assign ALUFunSel = and_19_out ? DecodedALUFunSel : 4'bz;  // Controlled_Buffer controlled_buffer_210
  not not_18 (not_18_out, TempFlagDest);
  not not_19 (not_19_out, TempFlagSrc1);
  and and_20 (and_20_out, or_13_out, not_19_out, not_18_out, TempFlagSrc2, T3);
  assign MUXASel = and_20_out ? 2'b00 : 2'bz;  // Controlled_Buffer controlled_buffer_211
  assign OutBSel = and_20_out ? {1'b0, Address[5:4]} : 3'bz;  // Controlled_Buffer controlled_buffer_212
  assign OutASel = and_20_out ? 3'b101 : 3'bz;  // Controlled_Buffer controlled_buffer_213
  assign MemSel = and_20_out ? 1'b1 : 1'bz;  // Controlled_Buffer controlled_buffer_214
  assign MemStr = and_20_out ? 1'b0 : 1'bz;  // Controlled_Buffer controlled_buffer_215
  assign MemLd = and_20_out ? 1'b0 : 1'bz;  // Controlled_Buffer controlled_buffer_216
  assign AddressRegSel = and_20_out ? 3'b111 : 3'bz;  // Controlled_Buffer controlled_buffer_217
  assign Reset = and_20_out ? 1'b1 : 1'bz;  // Controlled_Buffer controlled_buffer_218
  assign IREnable = and_20_out ? 1'b0 : 1'bz;  // Controlled_Buffer controlled_buffer_219
  assign RegFileRegSel = and_20_out ? multiplexer_11_out : 4'bz;  // Controlled_Buffer controlled_buffer_220
  assign RegFileTmpSel = and_20_out ? 4'b1111 : 4'bz;  // Controlled_Buffer controlled_buffer_221
  assign RegFileFunSel = and_20_out ? 2'b10 : 2'bz;  // Controlled_Buffer controlled_buffer_222
  assign ALUFunSel = and_20_out ? DecodedALUFunSel : 4'bz;  // Controlled_Buffer controlled_buffer_223
  and and_21 (and_21_out, TempFlagSrc1, or_14_out, T4, TempFlagDest);
  assign MUXBSel = and_21_out ? 2'b00 : 2'bz;  // Controlled_Buffer controlled_buffer_224
  assign OutASel = and_21_out ? 3'b110 : 3'bz;  // Controlled_Buffer controlled_buffer_225
  assign OutBSel = and_21_out ? 3'b111 : 3'bz;  // Controlled_Buffer controlled_buffer_226
  assign AddressRegSel = and_21_out ? multiplexer_12_out : 3'bz;  // Controlled_Buffer controlled_buffer_227
  assign RegFileRegSel = and_21_out ? 4'b1111 : 4'bz;  // Controlled_Buffer controlled_buffer_228
  assign RegFileTmpSel = and_21_out ? 4'b1111 : 4'bz;  // Controlled_Buffer controlled_buffer_229
  assign AddressFunSel = and_21_out ? 2'b10 : 2'bz;  // Controlled_Buffer controlled_buffer_230
  assign MemSel = and_21_out ? 1'b1 : 1'bz;  // Controlled_Buffer controlled_buffer_231
  assign MemStr = and_21_out ? 1'b0 : 1'bz;  // Controlled_Buffer controlled_buffer_232
  assign MemLd = and_21_out ? 1'b0 : 1'bz;  // Controlled_Buffer controlled_buffer_233
  assign Reset = and_21_out ? 1'b1 : 1'bz;  // Controlled_Buffer controlled_buffer_234
  assign IREnable = and_21_out ? 1'b0 : 1'bz;  // Controlled_Buffer controlled_buffer_235
  assign ALUFunSel = and_21_out ? DecodedALUFunSel : 4'bz;  // Controlled_Buffer controlled_buffer_236
  or or_15 (or_15_out, AND, OR, ADD, SUB);
  Decoder #(.select(4), .enable("false")) decoder_2 (
    .out0(BRA), .out1(LD), .out2(ST), .out3(MOV), .out4(AND), .out5(OR), .out6(NOT), .out7(ADD), .out8(SUB),
    .out9(LSL), .out10(LSR), .out11(PUL), .out12(PSH), .out13(INC), .out14(DEC), .out15(BNE),
    .sel(Instruction));
  or or_16 (or_16_out, INC, DEC);
  not not_20 (not_20_out, TempFlagSrc1);
  and and_22 (and_22_out, or_15_out, not_20_out, TempFlagSrc2, T2);
  assign MUXASel = and_22_out ? 2'b11 : 2'bz;  // Controlled_Buffer controlled_buffer_237
  assign OutCSel = and_22_out ? Address[1:0] : 2'bz;  // Controlled_Buffer controlled_buffer_238
  assign MemSel = and_22_out ? 1'b1 : 1'bz;  // Controlled_Buffer controlled_buffer_239
  assign MemStr = and_22_out ? 1'b0 : 1'bz;  // Controlled_Buffer controlled_buffer_240
  assign MemLd = and_22_out ? 1'b0 : 1'bz;  // Controlled_Buffer controlled_buffer_241
  assign AddressRegSel = and_22_out ? 3'b111 : 3'bz;  // Controlled_Buffer controlled_buffer_242
  assign Reset = and_22_out ? 1'b0 : 1'bz;  // Controlled_Buffer controlled_buffer_243
  assign IREnable = and_22_out ? 1'b0 : 1'bz;  // Controlled_Buffer controlled_buffer_244
  assign RegFileRegSel = and_22_out ? 4'b1111 : 4'bz;  // Controlled_Buffer controlled_buffer_245
  assign RegFileTmpSel = and_22_out ? 4'b1011 : 4'bz;  // Controlled_Buffer controlled_buffer_246
  assign RegFileFunSel = and_22_out ? 2'b10 : 2'bz;  // Controlled_Buffer controlled_buffer_247
  Multiplexer #(.select(2), .width(3), .enable("false")) multiplexer_13 (
    .in0(3'b011), .in1(3'b011), .in2(3'b101), .in3(3'b110), .out(multiplexer_13_out), .sel(DestReg[1:0]));
  not not_21 (not_21_out, AddressingMode);
  and and_23 (and_23_out, ST, not_21_out, T2);
  assign OutASel = and_23_out ? {1'b0, DestReg[1:0]} : 3'bz;  // Controlled_Buffer controlled_buffer_248
  assign OutDSel = and_23_out ? 2'b10 : 2'bz;  // Controlled_Buffer controlled_buffer_249
  assign MemSel = and_23_out ? 1'b1 : 1'bz;  // Controlled_Buffer controlled_buffer_250
  assign MemStr = and_23_out ? 1'b1 : 1'bz;  // Controlled_Buffer controlled_buffer_251
  assign MemLd = and_23_out ? 1'b0 : 1'bz;  // Controlled_Buffer controlled_buffer_252
  assign AddressRegSel = and_23_out ? 3'b111 : 3'bz;  // Controlled_Buffer controlled_buffer_253
  assign Reset = and_23_out ? 1'b1 : 1'bz;  // Controlled_Buffer controlled_buffer_254
  assign IREnable = and_23_out ? 1'b0 : 1'bz;  // Controlled_Buffer controlled_buffer_255
  assign RegFileRegSel = and_23_out ? 4'b1111 : 4'bz;  // Controlled_Buffer controlled_buffer_256
  assign RegFileTmpSel = and_23_out ? 4'b1111 : 4'bz;  // Controlled_Buffer controlled_buffer_257
  assign ALUFunSel = and_23_out ? DecodedALUFunSel : 4'bz;  // Controlled_Buffer controlled_buffer_258
  and and_24 (and_24_out, ST, AddressingMode, T2);
  assign Reset = and_24_out ? 1'b1 : 1'bz;  // Controlled_Buffer controlled_buffer_259
  not not_22 (not_22_out, TempFlagSrc1);
  or or_17 (or_17_out, AND, OR, ADD, SUB);
  and and_25 (and_25_out, MOV, not_22_out, TempFlagDest, T2);
  assign MUXBSel = and_25_out ? 2'b00 : 2'bz;  // Controlled_Buffer controlled_buffer_260
  assign OutASel = and_25_out ? {1'b0, Address[5:4]} : 3'bz;  // Controlled_Buffer controlled_buffer_261
  assign MemSel = and_25_out ? 1'b1 : 1'bz;  // Controlled_Buffer controlled_buffer_262
  assign MemStr = and_25_out ? 1'b0 : 1'bz;  // Controlled_Buffer controlled_buffer_263
  assign MemLd = and_25_out ? 1'b0 : 1'bz;  // Controlled_Buffer controlled_buffer_264
  assign AddressRegSel = and_25_out ? multiplexer_13_out : 3'bz;  // Controlled_Buffer controlled_buffer_265
  assign Reset = and_25_out ? 1'b1 : 1'bz;  // Controlled_Buffer controlled_buffer_266
  assign IREnable = and_25_out ? 1'b0 : 1'bz;  // Controlled_Buffer controlled_buffer_267
  assign RegFileRegSel = and_25_out ? 4'b1111 : 4'bz;  // Controlled_Buffer controlled_buffer_268
  assign RegFileTmpSel = and_25_out ? 4'b1111 : 4'bz;  // Controlled_Buffer controlled_buffer_269
  assign AddressFunSel = and_25_out ? 2'b10 : 2'bz;  // Controlled_Buffer controlled_buffer_270
  assign ALUFunSel = and_25_out ? DecodedALUFunSel : 4'bz;  // Controlled_Buffer controlled_buffer_271
  or or_18 (or_18_out, NOT, LSR, LSL);
  and and_26 (and_26_out, or_16_out, TempFlagSrc1, T3);
  assign MUXASel = and_26_out ? 2'b11 : 2'bz;  // Controlled_Buffer controlled_buffer_272
  assign OutCSel = and_26_out ? Address[5:4] : 2'bz;  // Controlled_Buffer controlled_buffer_273
  assign AddressRegSel = and_26_out ? 3'b111 : 3'bz;  // Controlled_Buffer controlled_buffer_274
  assign RegFileRegSel = and_26_out ? 4'b1111 : 4'bz;  // Controlled_Buffer controlled_buffer_275
  assign RegFileTmpSel = and_26_out ? 4'b1101 : 4'bz;  // Controlled_Buffer controlled_buffer_276
  assign RegFileFunSel = and_26_out ? 2'b10 : 2'bz;  // Controlled_Buffer controlled_buffer_277
  assign MemSel = and_26_out ? 1'b1 : 1'bz;  // Controlled_Buffer controlled_buffer_278
  assign MemStr = and_26_out ? 1'b0 : 1'bz;  // Controlled_Buffer controlled_buffer_279
  assign MemLd = and_26_out ? 1'b0 : 1'bz;  // Controlled_Buffer controlled_buffer_280
  assign Reset = and_26_out ? 1'b0 : 1'bz;  // Controlled_Buffer controlled_buffer_281
  assign IREnable = and_26_out ? 1'b0 : 1'bz;  // Controlled_Buffer controlled_buffer_282
  Multiplexer #(.select(2), .width(3), .enable("false")) multiplexer_14 (
    .in0(3'b011), .in1(3'b011), .in2(3'b101), .in3(3'b110), .out(multiplexer_14_out), .sel(DestReg[1:0]));
  Multiplexer #(.select(4), .width(4), .enable("false")) multiplexer_15 (
    .in0(4'b0000), .in1(4'b0000), .in2(4'b0000), .in3(4'b0000), .in4(4'b0111), .in5(4'b1000), .in6(4'b0010),
    .in7(4'b0100), .in8(4'b0110), .in9(4'b1010), .in10(4'b1011), .in11(4'b0000), .in12(4'b0000),
    .in13(4'b0100), .in14(4'b0110), .in15(4'b0000), .out(DecodedALUFunSel), .sel(Instruction));
  not not_23 (TempFlagSrc2, Address[2]);
  not not_24 (TempFlagSrc1, Address[6]);
  not not_25 (TempFlagDest, AddressingMode);
  Multiplexer #(.select(2), .width(3), .enable("false")) multiplexer_16 (
    .in0(3'b011), .in1(3'b011), .in2(3'b101), .in3(3'b110), .out(multiplexer_16_out), .sel(DestReg[1:0]));
  not not_26 (not_26_out, TempFlagSrc1);
  and and_27 (and_27_out, or_17_out, not_26_out, TempFlagDest, TempFlagSrc2, T3);
  assign MUXBSel = and_27_out ? 2'b00 : 2'bz;  // Controlled_Buffer controlled_buffer_283
  assign OutBSel = and_27_out ? {1'b0, Address[5:4]} : 3'bz;  // Controlled_Buffer controlled_buffer_284
  assign OutASel = and_27_out ? 3'b101 : 3'bz;  // Controlled_Buffer controlled_buffer_285
  assign MemSel = and_27_out ? 1'b1 : 1'bz;  // Controlled_Buffer controlled_buffer_286
  assign MemStr = and_27_out ? 1'b0 : 1'bz;  // Controlled_Buffer controlled_buffer_287
  assign MemLd = and_27_out ? 1'b0 : 1'bz;  // Controlled_Buffer controlled_buffer_288
  assign AddressRegSel = and_27_out ? multiplexer_14_out : 3'bz;  // Controlled_Buffer controlled_buffer_289
  assign Reset = and_27_out ? 1'b1 : 1'bz;  // Controlled_Buffer controlled_buffer_290
  assign IREnable = and_27_out ? 1'b0 : 1'bz;  // Controlled_Buffer controlled_buffer_291
  assign RegFileRegSel = and_27_out ? 4'b1111 : 4'bz;  // Controlled_Buffer controlled_buffer_292
  assign RegFileTmpSel = and_27_out ? 4'b1111 : 4'bz;  // Controlled_Buffer controlled_buffer_293
  assign AddressFunSel = and_27_out ? 2'b10 : 2'bz;  // Controlled_Buffer controlled_buffer_294
  assign ALUFunSel = and_27_out ? DecodedALUFunSel : 4'bz;  // Controlled_Buffer controlled_buffer_295
  not not_27 (not_27_out, TempFlagSrc1);
  and and_28 (and_28_out, or_18_out, not_27_out, TempFlagDest, T2);
  assign MUXBSel = and_28_out ? 2'b00 : 2'bz;  // Controlled_Buffer controlled_buffer_296
  assign OutASel = and_28_out ? {1'b0, Address[5:4]} : 3'bz;  // Controlled_Buffer controlled_buffer_297
  assign MemSel = and_28_out ? 1'b1 : 1'bz;  // Controlled_Buffer controlled_buffer_298
  assign MemStr = and_28_out ? 1'b0 : 1'bz;  // Controlled_Buffer controlled_buffer_299
  assign MemLd = and_28_out ? 1'b0 : 1'bz;  // Controlled_Buffer controlled_buffer_300
  assign AddressRegSel = and_28_out ? multiplexer_16_out : 3'bz;  // Controlled_Buffer controlled_buffer_301
  assign Reset = and_28_out ? 1'b1 : 1'bz;  // Controlled_Buffer controlled_buffer_302
  assign IREnable = and_28_out ? 1'b0 : 1'bz;  // Controlled_Buffer controlled_buffer_303
  assign RegFileRegSel = and_28_out ? 4'b1111 : 4'bz;  // Controlled_Buffer controlled_buffer_304
  assign RegFileTmpSel = and_28_out ? 4'b1111 : 4'bz;  // Controlled_Buffer controlled_buffer_305
  assign AddressFunSel = and_28_out ? 2'b10 : 2'bz;  // Controlled_Buffer controlled_buffer_306
  assign ALUFunSel = and_28_out ? DecodedALUFunSel : 4'bz;  // Controlled_Buffer controlled_buffer_307
  Decoder #(.select(2), .enable("false")) decoder_3 (
    .out0(decoder_3_out3[3]), .out1(decoder_3_out3[2]), .out2(decoder_3_out3[1]), .out3(decoder_3_out3[0]),
    .sel(DestReg[1:0]));
  Decoder #(.select(2), .enable("false")) decoder_4 (
    .out0(decoder_4_out3[3]), .out1(decoder_4_out3[2]), .out2(decoder_4_out3[1]), .out3(decoder_4_out3[0]),
    .sel(DestReg[1:0]));
  assign not_28_out = ~decoder_3_out3;  // NOT_Gate not_28, 4 bits wide
  not not_29 (not_29_out, AddressingMode);
  and and_29 (and_29_out, LD, not_29_out, T2);
  assign RegFileRegSel = and_29_out ? not_28_out : 4'bz;  // Controlled_Buffer controlled_buffer_308
  assign MUXASel = and_29_out ? 2'b01 : 2'bz;  // Controlled_Buffer controlled_buffer_309
  assign OutDSel = and_29_out ? 2'b10 : 2'bz;  // Controlled_Buffer controlled_buffer_310
  assign MemSel = and_29_out ? 1'b1 : 1'bz;  // Controlled_Buffer controlled_buffer_311
  assign MemStr = and_29_out ? 1'b0 : 1'bz;  // Controlled_Buffer controlled_buffer_312
  assign MemLd = and_29_out ? 1'b1 : 1'bz;  // Controlled_Buffer controlled_buffer_313
  assign AddressRegSel = and_29_out ? 3'b111 : 3'bz;  // Controlled_Buffer controlled_buffer_314
  assign Reset = and_29_out ? 1'b1 : 1'bz;  // Controlled_Buffer controlled_buffer_315
  assign IREnable = and_29_out ? 1'b0 : 1'bz;  // Controlled_Buffer controlled_buffer_316
  assign RegFileFunSel = and_29_out ? 2'b10 : 2'bz;  // Controlled_Buffer controlled_buffer_317
  assign RegFileTmpSel = and_29_out ? 4'b1111 : 4'bz;  // Controlled_Buffer controlled_buffer_318
  and and_30 (and_30_out, LD, AddressingMode, T2);
  assign not_30_out = ~decoder_4_out3;  // NOT_Gate not_30, 4 bits wide
  assign RegFileRegSel = and_30_out ? not_30_out : 4'bz;  // Controlled_Buffer controlled_buffer_319
  assign MUXASel = and_30_out ? 2'b10 : 2'bz;  // Controlled_Buffer controlled_buffer_320
  assign MemSel = and_30_out ? 1'b1 : 1'bz;  // Controlled_Buffer controlled_buffer_321
  assign MemStr = and_30_out ? 1'b0 : 1'bz;  // Controlled_Buffer controlled_buffer_322
  assign MemLd = and_30_out ? 1'b0 : 1'bz;  // Controlled_Buffer controlled_buffer_323
  assign AddressRegSel = and_30_out ? 3'b111 : 3'bz;  // Controlled_Buffer controlled_buffer_324
  assign Reset = and_30_out ? 1'b1 : 1'bz;  // Controlled_Buffer controlled_buffer_325
  assign IREnable = and_30_out ? 1'b0 : 1'bz;  // Controlled_Buffer controlled_buffer_326
  assign RegFileFunSel = and_30_out ? 2'b10 : 2'bz;  // Controlled_Buffer controlled_buffer_327
  assign RegFileTmpSel = and_30_out ? 4'b1111 : 4'bz;  // Controlled_Buffer controlled_buffer_328
  or or_19 (or_19_out, INC, DEC);
  Multiplexer #(.select(2), .width(4), .enable("false")) multiplexer_17 (
    .in0(4'b0111), .in1(4'b1011), .in2(4'b1101), .in3(4'b1110), .out(multiplexer_17_out), .sel(DestReg[1:0]));
  and and_31 (and_31_out, TempFlagSrc1, or_19_out, T4, not_31_out);
  assign MUXASel = and_31_out ? 2'b00 : 2'bz;  // Controlled_Buffer controlled_buffer_329
  assign OutASel = and_31_out ? 3'b110 : 3'bz;  // Controlled_Buffer controlled_buffer_330
  assign OutBSel = and_31_out ? 3'b111 : 3'bz;  // Controlled_Buffer controlled_buffer_331
  assign AddressRegSel = and_31_out ? 3'b111 : 3'bz;  // Controlled_Buffer controlled_buffer_332
  assign RegFileRegSel = and_31_out ? multiplexer_17_out : 4'bz;  // Controlled_Buffer controlled_buffer_333
  assign RegFileTmpSel = and_31_out ? 4'b1111 : 4'bz;  // Controlled_Buffer controlled_buffer_334
  assign RegFileFunSel = and_31_out ? 2'b10 : 2'bz;  // Controlled_Buffer controlled_buffer_335
  assign MemSel = and_31_out ? 1'b1 : 1'bz;  // Controlled_Buffer controlled_buffer_336
  assign MemStr = and_31_out ? 1'b0 : 1'bz;  // Controlled_Buffer controlled_buffer_337
  assign MemLd = and_31_out ? 1'b0 : 1'bz;  // Controlled_Buffer controlled_buffer_338
  assign Reset = and_31_out ? 1'b1 : 1'bz;  // Controlled_Buffer controlled_buffer_339
  assign IREnable = and_31_out ? 1'b0 : 1'bz;  // Controlled_Buffer controlled_buffer_340
  assign ALUFunSel = and_31_out ? DecodedALUFunSel : 4'bz;  // Controlled_Buffer controlled_buffer_341
  not not_31 (not_31_out, TempFlagDest);
  or or_20 (or_20_out, AND, OR, ADD, SUB);
  Multiplexer #(.select(2), .width(4), .enable("false")) multiplexer_18 (
    .in0(4'b0111), .in1(4'b1011), .in2(4'b1101), .in3(4'b1110), .out(multiplexer_18_out), .sel(DestReg[1:0]));
  not not_32 (not_32_out, TempFlagDest);
  not not_33 (not_33_out, TempFlagSrc2);
  and and_32 (and_32_out, or_20_out, TempFlagSrc1, not_32_out, not_33_out, T3);
  assign MUXASel = and_32_out ? 2'b00 : 2'bz;  // Controlled_Buffer controlled_buffer_342
  assign OutBSel = and_32_out ? 3'b100 : 3'bz;  // Controlled_Buffer controlled_buffer_343
  assign OutASel = and_32_out ? {1'b0, Address[1:0]} : 3'bz;  // Controlled_Buffer controlled_buffer_344
  assign MemSel = and_32_out ? 1'b1 : 1'bz;  // Controlled_Buffer controlled_buffer_345
  assign MemStr = and_32_out ? 1'b0 : 1'bz;  // Controlled_Buffer controlled_buffer_346
  assign MemLd = and_32_out ? 1'b0 : 1'bz;  // Controlled_Buffer controlled_buffer_347
  assign AddressRegSel = and_32_out ? 3'b111 : 3'bz;  // Controlled_Buffer controlled_buffer_348
  assign Reset = and_32_out ? 1'b1 : 1'bz;  // Controlled_Buffer controlled_buffer_349
  assign IREnable = and_32_out ? 1'b0 : 1'bz;  // Controlled_Buffer controlled_buffer_350
  assign RegFileRegSel = and_32_out ? multiplexer_18_out : 4'bz;  // Controlled_Buffer controlled_buffer_351
  assign RegFileTmpSel = and_32_out ? 4'b1111 : 4'bz;  // Controlled_Buffer controlled_buffer_352
  assign RegFileFunSel = and_32_out ? 2'b10 : 2'bz;  // Controlled_Buffer controlled_buffer_353
  assign ALUFunSel = and_32_out ? DecodedALUFunSel : 4'bz;  // Controlled_Buffer controlled_buffer_354
  or or_21 (or_21_out, AND, OR, ADD, SUB);
  Multiplexer #(.select(2), .width(3), .enable("false")) multiplexer_19 (
    .in0(3'b011), .in1(3'b011), .in2(3'b101), .in3(3'b110), .out(multiplexer_19_out), .sel(DestReg[1:0]));
  not not_34 (not_34_out, TempFlagSrc2);
  and and_33 (and_33_out, or_21_out, TempFlagSrc1, TempFlagDest, not_34_out, T3);
  assign MUXBSel = and_33_out ? 2'b00 : 2'bz;  // Controlled_Buffer controlled_buffer_355
  assign OutBSel = and_33_out ? 3'b100 : 3'bz;  // Controlled_Buffer controlled_buffer_356
  assign OutASel = and_33_out ? {1'b0, Address[1:0]} : 3'bz;  // Controlled_Buffer controlled_buffer_357
  assign MemSel = and_33_out ? 1'b1 : 1'bz;  // Controlled_Buffer controlled_buffer_358
  assign MemStr = and_33_out ? 1'b0 : 1'bz;  // Controlled_Buffer controlled_buffer_359
  assign MemLd = and_33_out ? 1'b0 : 1'bz;  // Controlled_Buffer controlled_buffer_360
  assign AddressRegSel = and_33_out ? multiplexer_19_out : 3'bz;  // Controlled_Buffer controlled_buffer_361
  assign Reset = and_33_out ? 1'b1 : 1'bz;  // Controlled_Buffer controlled_buffer_362
  assign IREnable = and_33_out ? 1'b0 : 1'bz;  // Controlled_Buffer controlled_buffer_363
  assign RegFileRegSel = and_33_out ? 4'b1111 : 4'bz;  // Controlled_Buffer controlled_buffer_364
  assign RegFileTmpSel = and_33_out ? 4'b1111 : 4'bz;  // Controlled_Buffer controlled_buffer_365
  assign AddressFunSel = and_33_out ? 2'b10 : 2'bz;  // Controlled_Buffer controlled_buffer_366
  assign ALUFunSel = and_33_out ? DecodedALUFunSel : 4'bz;  // Controlled_Buffer controlled_buffer_367
  or or_22 (or_22_out, AND, OR, ADD, SUB);
  and and_34 (and_34_out, or_22_out, TempFlagSrc1, T2);
  assign MUXASel = and_34_out ? 2'b11 : 2'bz;  // Controlled_Buffer controlled_buffer_368
  assign OutCSel = and_34_out ? Address[5:4] : 2'bz;  // Controlled_Buffer controlled_buffer_369
  assign MemSel = and_34_out ? 1'b1 : 1'bz;  // Controlled_Buffer controlled_buffer_370
  assign MemStr = and_34_out ? 1'b0 : 1'bz;  // Controlled_Buffer controlled_buffer_371
  assign MemLd = and_34_out ? 1'b0 : 1'bz;  // Controlled_Buffer controlled_buffer_372
  assign AddressRegSel = and_34_out ? 3'b111 : 3'bz;  // Controlled_Buffer controlled_buffer_373
  assign Reset = and_34_out ? 1'b0 : 1'bz;  // Controlled_Buffer controlled_buffer_374
  assign IREnable = and_34_out ? 1'b0 : 1'bz;  // Controlled_Buffer controlled_buffer_375
  assign RegFileRegSel = and_34_out ? 4'b1111 : 4'bz;  // Controlled_Buffer controlled_buffer_376
  assign RegFileTmpSel = and_34_out ? 4'b0111 : 4'bz;  // Controlled_Buffer controlled_buffer_377
  assign RegFileFunSel = and_34_out ? 2'b10 : 2'bz;  // Controlled_Buffer controlled_buffer_378
  or or_23 (or_23_out, AND, OR, ADD, SUB);
  Multiplexer #(.select(2), .width(4), .enable("false")) multiplexer_20 (
    .in0(4'b0111), .in1(4'b1011), .in2(4'b1101), .in3(4'b1110), .out(multiplexer_20_out), .sel(DestReg[1:0]));
  not not_35 (not_35_out, TempFlagDest);
  and and_35 (and_35_out, or_23_out, TempFlagSrc1, not_35_out, TempFlagSrc2, T4);
  assign MUXASel = and_35_out ? 2'b00 : 2'bz;  // Controlled_Buffer controlled_buffer_379
  assign OutBSel = and_35_out ? 3'b100 : 3'bz;  // Controlled_Buffer controlled_buffer_380
  assign OutASel = and_35_out ? 3'b101 : 3'bz;  // Controlled_Buffer controlled_buffer_381
  assign MemSel = and_35_out ? 1'b1 : 1'bz;  // Controlled_Buffer controlled_buffer_382
  assign MemStr = and_35_out ? 1'b0 : 1'bz;  // Controlled_Buffer controlled_buffer_383
  assign MemLd = and_35_out ? 1'b0 : 1'bz;  // Controlled_Buffer controlled_buffer_384
  assign AddressRegSel = and_35_out ? 3'b111 : 3'bz;  // Controlled_Buffer controlled_buffer_385
  assign Reset = and_35_out ? 1'b1 : 1'bz;  // Controlled_Buffer controlled_buffer_386
  assign IREnable = and_35_out ? 1'b0 : 1'bz;  // Controlled_Buffer controlled_buffer_387
  assign RegFileRegSel = and_35_out ? multiplexer_20_out : 4'bz;  // Controlled_Buffer controlled_buffer_388
  assign RegFileTmpSel = and_35_out ? 4'b1111 : 4'bz;  // Controlled_Buffer controlled_buffer_389
  assign RegFileFunSel = and_35_out ? 2'b10 : 2'bz;  // Controlled_Buffer controlled_buffer_390
  assign ALUFunSel = and_35_out ? DecodedALUFunSel : 4'bz;  // Controlled_Buffer controlled_buffer_391
  or or_24 (or_24_out, AND, OR, ADD, SUB);
  and and_36 (and_36_out, or_24_out, TempFlagSrc1, TempFlagSrc2, T3);
  assign MUXASel = and_36_out ? 2'b11 : 2'bz;  // Controlled_Buffer controlled_buffer_392
  assign OutCSel = and_36_out ? Address[1:0] : 2'bz;  // Controlled_Buffer controlled_buffer_393
  assign MemSel = and_36_out ? 1'b1 : 1'bz;  // Controlled_Buffer controlled_buffer_394
  assign MemStr = and_36_out ? 1'b0 : 1'bz;  // Controlled_Buffer controlled_buffer_395
  assign MemLd = and_36_out ? 1'b0 : 1'bz;  // Controlled_Buffer controlled_buffer_396
  assign AddressRegSel = and_36_out ? 3'b111 : 3'bz;  // Controlled_Buffer controlled_buffer_397
  assign Reset = and_36_out ? 1'b0 : 1'bz;  // Controlled_Buffer controlled_buffer_398
  assign IREnable = and_36_out ? 1'b0 : 1'bz;  // Controlled_Buffer controlled_buffer_399
  assign RegFileRegSel = and_36_out ? 4'b1111 : 4'bz;  // Controlled_Buffer controlled_buffer_400
  assign RegFileTmpSel = and_36_out ? 4'b1011 : 4'bz;  // Controlled_Buffer controlled_buffer_401
  assign RegFileFunSel = and_36_out ? 2'b10 : 2'bz;  // Controlled_Buffer controlled_buffer_402
  or or_25 (or_25_out, AND, OR, ADD, SUB);
  Multiplexer #(.select(2), .width(3), .enable("false")) multiplexer_21 (
    .in0(3'b011), .in1(3'b011), .in2(3'b101), .in3(3'b110), .out(multiplexer_21_out), .sel(DestReg[1:0]));
  and and_37 (and_37_out, or_25_out, TempFlagSrc1, TempFlagDest, TempFlagSrc2, T4);
  assign MUXBSel = and_37_out ? 2'b00 : 2'bz;  // Controlled_Buffer controlled_buffer_403
  assign OutBSel = and_37_out ? 3'b100 : 3'bz;  // Controlled_Buffer controlled_buffer_404
  assign OutASel = and_37_out ? 3'b101 : 3'bz;  // Controlled_Buffer controlled_buffer_405
  assign MemSel = and_37_out ? 1'b1 : 1'bz;  // Controlled_Buffer controlled_buffer_406
  assign MemStr = and_37_out ? 1'b0 : 1'bz;  // Controlled_Buffer controlled_buffer_407
  assign MemLd = and_37_out ? 1'b0 : 1'bz;  // Controlled_Buffer controlled_buffer_408
  assign AddressRegSel = and_37_out ? multiplexer_21_out : 3'bz;  // Controlled_Buffer controlled_buffer_409
  assign Reset = and_37_out ? 1'b1 : 1'bz;  // Controlled_Buffer controlled_buffer_410
  assign IREnable = and_37_out ? 1'b0 : 1'bz;  // Controlled_Buffer controlled_buffer_411
  assign RegFileRegSel = and_37_out ? 4'b1111 : 4'bz;  // Controlled_Buffer controlled_buffer_412
  assign RegFileTmpSel = and_37_out ? 4'b1111 : 4'bz;  // Controlled_Buffer controlled_buffer_413
  assign AddressFunSel = and_37_out ? 2'b10 : 2'bz;  // Controlled_Buffer controlled_buffer_414
  assign ALUFunSel = and_37_out ? DecodedALUFunSel : 4'bz;  // Controlled_Buffer controlled_buffer_415

  // Other names for the same wires on the sheet: Instruction[11:0] = {DestReg[3], AddressingMode, DestReg[1:0], Address};
  //   RegSel[1:0] = DestReg[1:0]; SrcReg1[3:0] = Address[7:4]; SrcReg2[3:0] = Address[3:0];
  //   DestReg[2] = AddressingMode; OpCode[3:0] = Instruction; ZCNO[3:0] = {Z, C, N, O}

  // Notes on the sheet:
  //   IMT2:PC <- Value, SC <- 0
  //   MOV
  //   BRA   BNE
  //   (else Z = 1)ZT2:SC <- 0
  //   IM' T2:SC <- 0
  //   SRCREG1 and DSTREG are belong to Address Register File
  //   SRCREG1 and DSTREG are belong to Address Register File
  //   INC    DEC
  //   SRCREG1ıs belong to Regıster Fıle and DSTREG is belong to Register File
  //   SRC1 =REG SRC2 = REG DSTCREG = ADDRESS 
  //   TempFlagSrc1'TempFlagSrc2'TempFlagDestT2:
  //   DESTREG <- SRCREG2 AND SRCREG1
  //   DESTREG <- SRCREG2 OR SRCREG1
  //   DESTREG <- SRCREG2 + SRCREG1
  //   DESTREG <- SRCREG2 - SRCREG1
  //   CPU
  //   (if Z=0) IMZ'T2: PC <- Value, SC <- 0
  //   NOT    LSL    LSR
  //   T2: T1 <- SRCREG1
  //   SRCREG1 is  belong to Address Register File
  //   T3: DESTREG <- (NOT or LSR or LSL)T1
  //   T3:DESTREG <- SRCREG + 1/SRCREG - 1, SC <- 0 
  //   AND    OR    ADD    SUB
  //   SRCREG1ıs belong to Address Regıster Fıle and DSTREG is belong to Register File
  //   SRCREG1ıs belong to Address Regıster Fıle and DSTREG is belong to Register File
  //   SRC1 =REG SRC2 = REG DSTCREG = REG 
  //   TempFlagSrc1'TempFlagSrc2'TempFlagDest'T2:
  //   DESTREG <- SRCREG2 AND SRCREG1
  //   DESTREG <- SRCREG2 OR SRCREG1
  //   DESTREG <- SRCREG2 + SRCREG1
  //   DESTREG <- SRCREG2 - SRCREG1
  //   T2:M[SP] <- Rx, SP <- SP - 1, SC <- 0
  //   SRCREG1ıs belong to Regıster Fıle and DSTREG is belong to Address  Register File
  //   T0: IR(0-7) <- M[PC], PC <- PC+1
  //   PSH           PUL
  //   T2: DESTREG <- SRCREG1
  //   FETCH 
  //   T2: SP <- SP + 1
  //   T1: IR(8-15) <- M[PC], PC <- PC+1
  //   T3: Rx <- M[SP], SC <- 0
  //   SRCREG1ıs belong to Regıster Fıle and DSTREG is belong to Register File
  //   SRCREG1ıs belong to Regıster Fıle and DSTREG is belong to Register File
  //   T2:T4 <- 01 
  //   SRCREG1 and DSTREG are belong to Address Register File
  //   DSTCREG = REG 
  //   TempFlagSrc1'TempFlagSrc2TempFlagDest'T3:
  //   DESTREG <- T2 AND SRCREG1
  //   DESTREG <- T2 OR SRCREG1
  //   DESTREG <- T2 + SRCREG1
  //   DESTREG <- T2 - SRCREG1
  //   SRC1 =REG   SRC2 = ADDRESS  
  //   T2: DESTREG <- (NOT or LSR or LSL)SRCREG1
  //   TempFlagSrc1'TempFlagSrc2T2: 
  //   T2 <- SRCREG2
  //   DT2:Value <- Rx, SC <- 0
  //   D'T2:SC <- 0
  //   T3:T3<-  SRCREG  
  //   SRCREG1 belongs to Address Register File
  //   T4:DESTREG<-  T3 + T4 / T3 - T4 , SC <- 0 
  //   SRCREG1ıs belong to Regıster Fıle and DSTREG is belong to Address  Register File
  //   DECODE
  //   Decode(OpCode), ALU operations
  //   DSTCREG = ADDRESS 
  //   TempFlagSrc1'TempFlagSrc2TempFlagDestT3:
  //   DESTREG <- T2 AND SRCREG1
  //   DESTREG <- T2 OR SRCREG1
  //   DESTREG <- T2 + SRCREG1
  //   DESTREG <- T2 - SRCREG1
  //   ST           LD
  //   SRCREG1ıs belong to Regıster Fıle and DSTREG is belong to Address  Register File
  //   DT2: Rx <- M[AR], SC <- 0
  //   IMT2: Rx <- ADRESS Field, SC <- 0
  //   SRCREG1ıs belong to Address Regıster Fıle and DSTREG is belong to Register File
  //   DSTCREG = REG 
  //   TempFlagSrc1TempFlagSrc2'TempFlagDest'T3:
  //   DESTREG <- SRCREG2 AND T1
  //   DESTREG <- SRCREG2 OR T1
  //   DESTREG <- SRCREG2 + T1
  //   DESTREG <- SRCREG2 - T1
  //   DSTCREG = ADDRESS 
  //   TempFlagSrc1TempFlagSrc2'TempFlagDestT3:
  //   DESTREG <- SRCREG2 AND T1
  //   DESTREG <- SRCREG2 OR T1
  //   DESTREG <- SRCREG2 + T1
  //   DESTREG <- SRCREG2 - T1
  //   SRC1 = ADDRESS    
  //   TempFlagSrc1T2: 
  //   T1 <- SRCREG1
  //   DSTCREG = REG 
  //   TempFlagSrc1TempFlagSrc2TempFlagDest'T4:
  //   DESTREG <- T2 AND T1
  //   DESTREG <- T2 OR T1
  //   DESTREG <- T2 + T1
  //   DESTREG <- T2 - T1
  //   SRC2 = ADDRESS    
  //   TempFlagSrc1TempFlagSrc2T3: 
  //   T2 <- SRCREG2
  //   DSTCREG = ADDRESS 
  //   TempFlagSrc1TempFlagSrc2TempFlagDestT4:
  //   DESTREG <- T2 AND T1
  //   DESTREG <- T2 OR T1
  //   DESTREG <- T2 + T1
  //   DESTREG <- T2 - T1
endmodule

module SequentialCounter (
  input  CLK,
  input  Reset,
  output T0,
  output T1,
  output T2,
  output T3,
  output T4,
  output T5,
  output T6,
  output T7
);

  wire [1:0] multiplexer_1_out;
  wire [7:0] Sequential_Counter_q;

  Multiplexer #(.width(2), .enable("false")) multiplexer_1 (
    .in0(2'b01), .in1(2'b11), .out(multiplexer_1_out), .sel(Reset));
  _8_bit_Register_Part1a__main Sequential_Counter (
    .FunSel(multiplexer_1_out), .E(1'b1), .CLK(CLK), .Q(Sequential_Counter_q));  // open: I
  Decoder #(.select(3), .enable("false")) decoder_1 (
    .out0(T0), .out1(T1), .out2(T2), .out3(T3), .out4(T4), .out5(T5), .out6(T6), .out7(T7),
    .sel(Sequential_Counter_q[2:0]));
endmodule
