// Logisim project WholeSystem(Part4).circ as structural Verilog: 1 circuit, main circuit main
module main (
  input  CLK,
  input  [3:0] ALUFunSel,
  input  [2:0] OutASel,
  input  [2:0] OutBSel,
  input  [1:0] RegFileFunSel,
  input  [3:0] RegFileRegSel,
  input  [3:0] RegFileTmpSel,
  input  [1:0] MUXASel,
  input  [1:0] MUXBSel,
  input  [1:0] OutCSel,
  input  [1:0] OutDSel,
  input  MemStr,
  input  MemSel,
  input  MemLd,
  input  MemClr,
  input  [1:0] AddressFunSel,
  input  [2:0] AddressRegSel,
  input  L_H,
  input  [1:0] IRFunSel,
  input  IREnable,
  output [3:0] ZCNO,
  output [15:0] Instruction
);

  wire [3:0] ALU_zcno;
  wire [7:0] Adress_Register_File_outc, Adress_Register_File_outd, ALU_output, multiplexer_1_out,
       multiplexer_2_out, ram_1_data, Register_File_outa, Register_File_outb;

  Multiplexer #(.select(2), .width(8), .enable("false")) multiplexer_1 (
    .in0(ALU_output), .in1(ram_1_data), .in2(Instruction[7:0]), .in3(Adress_Register_File_outc),
    .out(multiplexer_1_out), .sel(MUXASel));
  _16_bit_InstructionRegister_Part1b__main Instruction_Register (
    .FunSel(IRFunSel), .L_nH(L_H), .I(ram_1_data), .E(IREnable), .CLK(CLK), .IRout(Instruction));
  Multiplexer #(.select(2), .width(8), .enable("false")) multiplexer_2 (
    .in0(ALU_output), .in1(ram_1_data), .in2(Instruction[7:0]), .in3(Adress_Register_File_outc),
    .out(multiplexer_2_out), .sel(MUXBSel));
  _8_bit_GeneralRegisterFile_Part2a__main Register_File (
    .RegSel(RegFileRegSel), .CLK(CLK), .FunSel(RegFileFunSel), .Input(multiplexer_1_out), .OutASel(OutASel),
    .OutBSel(OutBSel), .TempSel(RegFileTmpSel), .OutA(Register_File_outa), .OutB(Register_File_outb));
  _8_bit_AdressRegisterFile_Part2b__main Adress_Register_File (
    .RegSel(AddressRegSel), .Input(multiplexer_2_out), .OutCSel(OutCSel), .FunSel(AddressFunSel),
    .OutDSel(OutDSel), .CLK(CLK), .OutC(Adress_Register_File_outc), .OutD(Adress_Register_File_outd));
  Hex_Digit_Display hex_digit_display_1 (.value(Instruction[15:12]));  // open: dp
  Hex_Digit_Display hex_digit_display_2 (.value(Instruction[11:8]));  // open: dp
  Hex_Digit_Display hex_digit_display_3 (.value(Instruction[7:4]));  // open: dp
  Hex_Digit_Display hex_digit_display_4 (.value(Instruction[3:0]));  // open: dp
  ALU ALU (
    .A(Register_File_outa), .B(Register_File_outb), .Cin(ZCNO[2]), .ZCNO(ALU_zcno), .Output(ALU_output),
    .FunSel(ALUFunSel));
  ZCNO zcno_1 (.ZCNO_IN(ALU_zcno), .CLK(CLK), .ZCNO_OUT(ZCNO));
  RAM #(.bus("separate")) ram_1 (
    .addr(Adress_Register_File_outd), .din(ALU_output), .data(ram_1_data), .str(MemStr), .sel(MemSel),
    .clk(CLK), .ld(MemLd), .clr(MemClr));
endmodule
